// Logisim project CUPU.circ as structural Verilog
module alu (
  input  enable,
  input  [4:0] op,
  input  [31:0] a,
  input  [31:0] b,
  output [31:0] result,
  output [7:0] flags
);

  wire adder_1_cout, adder_2_cout, delay_1_out_2, subtractor_1_bout, subtractor_2_bout;
  wire [4:0] bit_extender_1_out, bit_extender_2_out;
  wire [7:0] multiplexer_1_out_2;
  wire [30:1] multiplexer_1_out;
  wire [31:0] adder_1_out, adder_2_out, and_1_out, divider_1_out, divider_1_rem, fptoint_1_p1, fptoint_1_p2,
       multiplier_1_cout, multiplier_1_out, nand_1_out, negator_1_out, nor_1_out, not_1_out, or_1_out,
       shifter_1_out, shifter_2_out, subtractor_1_out, subtractor_2_out, xnor_1_out, xor_1_out;

  Bit_Extender #(.in_width(32), .out_width(5)) bit_extender_1 (.in(b), .out(bit_extender_1_out));
  Bit_Extender #(.in_width(32), .out_width(5)) bit_extender_2 (.in(b), .out(bit_extender_2_out));
  // Random #(.width(32)) random_1: pin names not known; wires that end beside it: a, enable
  Adder #(.width(32)) adder_1 (.a(a), .b(b), .out(adder_1_out), .cout(adder_1_cout));  // open: cin
  Subtractor #(.width(32)) subtractor_1 (.a(a), .b(b), .out(subtractor_1_out), .bout(subtractor_1_bout));  // open: bin
  Multiplier #(.width(32)) multiplier_1 (.a(a), .b(b), .out(multiplier_1_out), .cout(multiplier_1_cout));  // open: cin
  Divider #(.width(32)) divider_1 (.a(a), .b(b), .out(divider_1_out), .rem(divider_1_rem));  // open: upper
  Adder #(.width(32)) adder_2 (.a(a), .b(32'h1), .out(adder_2_out), .cout(adder_2_cout));  // open: cin
  Subtractor #(.width(32)) subtractor_2 (
    .a(a), .b(32'h1), .out(subtractor_2_out), .bout(subtractor_2_bout));  // open: bin
  Negator #(.width(32)) negator_1 (.in(a), .out(negator_1_out));
  Shifter #(.width(32)) shifter_1 (.in(a), .\dist (bit_extender_1_out), .out(shifter_1_out));
  Shifter #(.shift("lr"), .width(32)) shifter_2 (.in(a), .\dist (bit_extender_2_out), .out(shifter_2_out));
  assign or_1_out = a | b;  // OR_Gate or_1, 32 bits wide
  assign and_1_out = a & b;  // AND_Gate and_1, 32 bits wide
  assign xor_1_out = a ^ b;  // XOR_Gate xor_1, 32 bits wide
  assign not_1_out = ~a;  // NOT_Gate not_1, 32 bits wide
  assign nor_1_out = ~(a | b);  // NOR_Gate nor_1, 32 bits wide
  assign nand_1_out = ~(a & b);  // NAND_Gate nand_1, 32 bits wide
  assign xnor_1_out = ~(a ^ b);  // XNOR_Gate xnor_1, 32 bits wide
  // FPToInt #(.width(32)) fptoint_1: pin names not known; wires that end beside it: fptoint_1_p1, fptoint_1_p2
  Multiplexer #(.select(5), .width(32)) multiplexer_1 (
    .in0(adder_1_out), .in1(subtractor_1_out), .in2(multiplier_1_out), .in3(divider_1_out),
    .in4(adder_2_out), .in5(subtractor_2_out), .in6(negator_1_out), .in7(shifter_1_out), .in8(shifter_2_out),
    .in9(or_1_out), .in10(and_1_out), .in11(xor_1_out), .in12(not_1_out), .in13(nor_1_out),
    .in14(nand_1_out), .in15(xnor_1_out), .in16(fptoint_1_p1), .in17(fptoint_1_p2), .in18(a),
    .in19(multiplier_1_cout), .in20(divider_1_rem),
    .out({multiplexer_1_out_2[1], multiplexer_1_out, multiplexer_1_out_2[0]}), .sel(op));  // open: in21, in22, in23, in24, in25, in26, in27, in28, in29, in30, in31
  Multiplexer #(.select(5)) multiplexer_2 (
    .in0(adder_1_cout), .in1(subtractor_1_bout), .in4(adder_2_cout), .in5(subtractor_2_bout),
    .out(multiplexer_1_out_2[3]), .sel(op));  // open: in2, in3, in6, in7, in8, in9, in10, in11, in12, in13, in14, in15, in16, in17, in18, in19, in20, in21, in22, in23, in24, in25, in26, in27, in28, in29, in30, in31
  Comparator #(.width(32)) comparator_1 (
    .a({multiplexer_1_out_2[1], multiplexer_1_out, multiplexer_1_out_2[0]}), .b({32{1'b0}}),
    .eq(multiplexer_1_out_2[2]));  // open: gt, lt
  Comparator #(.width(32)) comparator_2 (
    .a({multiplexer_1_out_2[1], multiplexer_1_out, multiplexer_1_out_2[0]}), .b({32{1'b1}}),
    .eq(multiplexer_1_out_2[4]));  // open: gt, lt
  Comparator #(.width(32)) comparator_3 (
    .a(a), .b(b), .gt(multiplexer_1_out_2[5]), .eq(multiplexer_1_out_2[6]), .lt(multiplexer_1_out_2[7]));
  Register #(.width(32)) register_1 (
    .D({multiplexer_1_out_2[1], multiplexer_1_out, multiplexer_1_out_2[0]}), .Q(result), .clk(delay_1_out_2));  // open: en, clr
  Register register_2 (.D(multiplexer_1_out_2), .Q(flags), .clk(delay_1_out_2));  // open: en, clr
  delay delay_1 (.in_1(enable), .out_2(delay_1_out_2));
endmodule

module regs (
  input  [7:0] s0_sel,
  input  [7:0] s1_sel,
  input  [7:0] dest_sel,
  input  [31:0] data,
  input  load,
  output [31:0] out_6,
  output [31:0] out_7
);

  wire decoder_1_out0, decoder_1_out1, decoder_1_out2, decoder_1_out3, decoder_1_out4, decoder_1_out5,
       decoder_1_out6, decoder_1_out7, decoder_1_out8, decoder_1_out9, decoder_1_out10, decoder_1_out11,
       decoder_1_out12, decoder_1_out13, decoder_1_out14, decoder_1_out15, delay_1_out_2;
  wire [3:0] bit_extender_1_out, bit_extender_2_out, bit_extender_3_out;
  wire [31:0] register_1_q, register_2_q, register_3_q, register_4_q, register_5_q, register_6_q,
       register_7_q, register_8_q, register_9_q, register_10_q, register_11_q, register_12_q, register_13_q,
       register_14_q, register_15_q, register_16_q;

  Bit_Extender #(.out_width(4)) bit_extender_1 (.in(s0_sel), .out(bit_extender_1_out));
  Bit_Extender #(.out_width(4)) bit_extender_2 (.in(s1_sel), .out(bit_extender_2_out));
  Bit_Extender #(.out_width(4)) bit_extender_3 (.in(dest_sel), .out(bit_extender_3_out));
  Decoder #(.select(4)) decoder_1 (
    .out0(decoder_1_out0), .out1(decoder_1_out1), .out2(decoder_1_out2), .out3(decoder_1_out3),
    .out4(decoder_1_out4), .out5(decoder_1_out5), .out6(decoder_1_out6), .out7(decoder_1_out7),
    .out8(decoder_1_out8), .out9(decoder_1_out9), .out10(decoder_1_out10), .out11(decoder_1_out11),
    .out12(decoder_1_out12), .out13(decoder_1_out13), .out14(decoder_1_out14), .out15(decoder_1_out15),
    .sel(bit_extender_3_out), .en(delay_1_out_2));
  delay delay_1 (.in_1(load), .out_2(delay_1_out_2));
  Register #(.width(32)) register_1 (.D(data), .Q(register_1_q), .clk(decoder_1_out0));  // open: en, clr
  Register #(.width(32)) register_2 (.D(data), .Q(register_2_q), .clk(decoder_1_out1));  // open: en, clr
  Register #(.width(32)) register_3 (.D(data), .Q(register_3_q), .clk(decoder_1_out2));  // open: en, clr
  Register #(.width(32)) register_4 (.D(data), .Q(register_4_q), .clk(decoder_1_out3));  // open: en, clr
  Register #(.width(32)) register_5 (.D(data), .Q(register_5_q), .clk(decoder_1_out4));  // open: en, clr
  Register #(.width(32)) register_6 (.D(data), .Q(register_6_q), .clk(decoder_1_out5));  // open: en, clr
  Register #(.width(32)) register_7 (.D(data), .Q(register_7_q), .clk(decoder_1_out6));  // open: en, clr
  Register #(.width(32)) register_8 (.D(data), .Q(register_8_q), .clk(decoder_1_out7));  // open: en, clr
  Register #(.width(32)) register_9 (.D(data), .Q(register_9_q), .clk(decoder_1_out8));  // open: en, clr
  Register #(.width(32)) register_10 (.D(data), .Q(register_10_q), .clk(decoder_1_out9));  // open: en, clr
  Register #(.width(32)) register_11 (.D(data), .Q(register_11_q), .clk(decoder_1_out10));  // open: en, clr
  Register #(.width(32)) register_12 (.D(data), .Q(register_12_q), .clk(decoder_1_out11));  // open: en, clr
  Register #(.width(32)) register_13 (.D(data), .Q(register_13_q), .clk(decoder_1_out12));  // open: en, clr
  Register #(.width(32)) register_14 (.D(data), .Q(register_14_q), .clk(decoder_1_out13));  // open: en, clr
  Register #(.width(32)) register_15 (.D(data), .Q(register_15_q), .clk(decoder_1_out14));  // open: en, clr
  Register #(.width(32)) register_16 (.D(data), .Q(register_16_q), .clk(decoder_1_out15));  // open: en, clr
  Multiplexer #(.select(4), .width(32)) multiplexer_1 (
    .in0(register_1_q), .in1(register_2_q), .in2(register_3_q), .in3(register_4_q), .in4(register_5_q),
    .in5(register_6_q), .in6(register_7_q), .in7(register_8_q), .in8(register_9_q), .in9(register_10_q),
    .in10(register_11_q), .in11(register_12_q), .in12(register_13_q), .in13(register_14_q),
    .in14(register_15_q), .in15(register_16_q), .out(out_6), .sel(bit_extender_1_out));
  Multiplexer #(.select(4), .width(32)) multiplexer_2 (
    .in0(register_1_q), .in1(register_2_q), .in2(register_3_q), .in3(register_4_q), .in4(register_5_q),
    .in5(register_6_q), .in6(register_7_q), .in7(register_8_q), .in8(register_9_q), .in9(register_10_q),
    .in10(register_11_q), .in11(register_12_q), .in12(register_13_q), .in13(register_14_q),
    .in14(register_15_q), .in15(register_16_q), .out(out_7), .sel(bit_extender_2_out));
endmodule

module delay (
  input  in_1,
  output out_2
);

  wire buffer_1_out, buffer_2_out, buffer_3_out, buffer_4_out, buffer_5_out, buffer_6_out, buffer_7_out,
       buffer_8_out, buffer_9_out, buffer_10_out, buffer_11_out, buffer_12_out, buffer_13_out, buffer_14_out,
       buffer_15_out, buffer_16_out, buffer_17_out, buffer_18_out, buffer_19_out, buffer_20_out,
       buffer_21_out, buffer_22_out, buffer_23_out, buffer_24_out, buffer_25_out, buffer_26_out,
       buffer_27_out, buffer_28_out, buffer_29_out, buffer_30_out, buffer_31_out, buffer_32_out,
       buffer_33_out, buffer_34_out, buffer_35_out, buffer_36_out, buffer_37_out, buffer_38_out,
       buffer_39_out, buffer_40_out, buffer_41_out, buffer_42_out, buffer_43_out, buffer_44_out,
       buffer_45_out, buffer_46_out, buffer_47_out;

  buf buffer_1 (buffer_1_out, in_1);
  buf buffer_2 (buffer_2_out, buffer_1_out);
  buf buffer_3 (buffer_3_out, buffer_2_out);
  buf buffer_4 (buffer_4_out, buffer_5_out);
  buf buffer_5 (buffer_5_out, buffer_6_out);
  buf buffer_6 (buffer_6_out, buffer_7_out);
  buf buffer_7 (buffer_7_out, buffer_15_out);
  buf buffer_8 (buffer_8_out, buffer_4_out);
  buf buffer_9 (buffer_9_out, buffer_8_out);
  buf buffer_10 (buffer_10_out, buffer_9_out);
  buf buffer_11 (buffer_11_out, buffer_3_out);
  buf buffer_12 (buffer_12_out, buffer_11_out);
  buf buffer_13 (buffer_13_out, buffer_12_out);
  buf buffer_14 (buffer_14_out, buffer_13_out);
  buf buffer_15 (buffer_15_out, buffer_16_out);
  buf buffer_16 (buffer_16_out, buffer_17_out);
  buf buffer_17 (buffer_17_out, buffer_18_out);
  buf buffer_18 (buffer_18_out, buffer_27_out);
  buf buffer_19 (buffer_19_out, buffer_10_out);
  buf buffer_20 (buffer_20_out, buffer_19_out);
  buf buffer_21 (buffer_21_out, buffer_20_out);
  buf buffer_22 (buffer_22_out, buffer_21_out);
  buf buffer_23 (buffer_23_out, buffer_14_out);
  buf buffer_24 (buffer_24_out, buffer_23_out);
  buf buffer_25 (buffer_25_out, buffer_24_out);
  buf buffer_26 (buffer_26_out, buffer_25_out);
  buf buffer_27 (buffer_27_out, buffer_28_out);
  buf buffer_28 (buffer_28_out, buffer_29_out);
  buf buffer_29 (buffer_29_out, buffer_30_out);
  buf buffer_30 (buffer_30_out, buffer_39_out);
  buf buffer_31 (buffer_31_out, buffer_22_out);
  buf buffer_32 (buffer_32_out, buffer_31_out);
  buf buffer_33 (buffer_33_out, buffer_32_out);
  buf buffer_34 (buffer_34_out, buffer_33_out);
  buf buffer_35 (buffer_35_out, buffer_26_out);
  buf buffer_36 (buffer_36_out, buffer_35_out);
  buf buffer_37 (buffer_37_out, buffer_36_out);
  buf buffer_38 (buffer_38_out, buffer_37_out);
  buf buffer_39 (buffer_39_out, buffer_40_out);
  buf buffer_40 (buffer_40_out, buffer_41_out);
  buf buffer_41 (buffer_41_out, buffer_42_out);
  buf buffer_42 (buffer_42_out, buffer_47_out);
  buf buffer_43 (buffer_43_out, buffer_34_out);
  buf buffer_44 (buffer_44_out, buffer_43_out);
  buf buffer_45 (buffer_45_out, buffer_44_out);
  buf buffer_46 (buffer_46_out, buffer_45_out);
  buf buffer_47 (buffer_47_out, buffer_38_out);
  buf buffer_48 (out_2, buffer_46_out);
endmodule

module cpu (
  input  [7:0] in_1,
  output [7:0] out_2,
  output [31:0] out_3,
  output out_4
);

  wire decoder_1_out7, decoder_1_out8, decoder_1_out9, decoder_1_out10, decoder_1_out11, decoder_1_out12,
       decoder_1_out13, decoder_1_out14, decoder_1_out15, undriven, undriven_2, undriven_3, undriven_5,
       undriven_6, undriven_7, undriven_8, undriven_9, undriven_11;
  wire [2:0] undriven_10;
  wire [3:0] undriven_4;
  wire [4:0] bit_extender_1_out;
  wire [7:0] alu_1_flags, dest_q, inst_extra_q, inst_q, register_2_q, register_3_q, register_4_q,
       register_5_q, s0_q, s1_q;
  wire [31:0] a_max_q, address_q, alu_1_result, bit_extender_2_out, fp_q, multiplexer_3_out, register_1_q,
       regs_1_out_6, regs_1_out_7, sp_q, subtractor_1_out, subtractor_2_out;

  Multiplexer #(.width(32)) multiplexer_1 (.in0(address_q), .in1(subtractor_2_out), .out(out_3));  // open: sel
  Register #(.width(32)) a_max (.D(multiplexer_3_out), .Q(a_max_q), .clk(undriven));  // open: en, clr
  Register #(.width(32)) fp (.D(multiplexer_3_out), .Q(fp_q), .clk(undriven_2));  // open: en, clr
  Decoder #(.select(4)) decoder_1 (
    .out7(decoder_1_out7), .out8(decoder_1_out8), .out9(decoder_1_out9), .out10(decoder_1_out10),
    .out11(decoder_1_out11), .out12(decoder_1_out12), .out13(decoder_1_out13), .out14(decoder_1_out14),
    .out15(decoder_1_out15), .sel(undriven_4), .en(undriven_5));  // open: out0, out1, out2, out3, out4, out5, out6
  Subtractor #(.width(32)) subtractor_1 (.a(a_max_q), .b(fp_q), .out(subtractor_1_out));  // open: bin, bout
  Subtractor #(.width(32)) subtractor_2 (.a(subtractor_1_out), .b(sp_q), .out(subtractor_2_out));  // open: bin, bout
  Register #(.width(32)) sp (.D(multiplexer_3_out), .Q(sp_q), .clk(undriven_3));  // open: en, clr
  Register inst (.D(in_1), .Q(inst_q), .clk(decoder_1_out7));  // open: en, clr
  Register inst_extra (.D(in_1), .Q(inst_extra_q), .clk(decoder_1_out8));  // open: en, clr
  Register #(.width(32)) address (.D(multiplexer_3_out), .Q(address_q), .clk(undriven_6));  // open: en, clr
  Register s0 (.D(in_1), .Q(s0_q), .clk(decoder_1_out9));  // open: en, clr
  Register #(.width(32)) register_1 (.D(multiplexer_3_out), .Q(register_1_q), .clk(undriven_7));  // open: en, clr
  Register s1 (.D(in_1), .Q(s1_q), .clk(decoder_1_out10));  // open: en, clr
  Multiplexer #(.select(2), .width(8)) multiplexer_2 (
    .in0(register_1_q[31:24]), .in1(register_1_q[23:16]), .in2(register_1_q[15:8]), .in3(register_1_q[7:0]),
    .out(out_2));  // open: sel
  Register dest (.D(in_1), .Q(dest_q), .clk(decoder_1_out11));  // open: en, clr
  Register register_2 (.D(in_1), .Q(register_2_q), .clk(decoder_1_out15), .clr(undriven_11));  // open: en
  Register register_3 (.D(in_1), .Q(register_3_q), .clk(decoder_1_out14), .clr(undriven_11));  // open: en
  Register register_4 (.D(in_1), .Q(register_4_q), .clk(decoder_1_out13), .clr(undriven_11));  // open: en
  Multiplexer #(.select(3), .width(32)) multiplexer_3 (
    .in0({register_2_q, register_3_q, register_4_q, register_5_q}), .in1(regs_1_out_6), .in2(alu_1_result),
    .in3(bit_extender_2_out), .in4(sp_q), .in5(fp_q), .out(multiplexer_3_out), .sel(undriven_10));  // open: in6, in7
  regs regs_1 (
    .s0_sel(s0_q), .s1_sel(s1_q), .dest_sel(dest_q), .data(multiplexer_3_out), .load(undriven_9),
    .out_6(regs_1_out_6), .out_7(regs_1_out_7));
  Register register_5 (.D(in_1), .Q(register_5_q), .clk(decoder_1_out12), .clr(undriven_11));  // open: en
  Bit_Extender #(.out_width(5)) bit_extender_1 (.in(inst_extra_q), .out(bit_extender_1_out));
  alu alu_1 (
    .enable(undriven_8), .op(bit_extender_1_out), .a(regs_1_out_6), .b(regs_1_out_7), .result(alu_1_result),
    .flags(alu_1_flags));
  assign bit_extender_2_out = {{24{alu_1_flags[7]}}, alu_1_flags};  // Bit_Extender bit_extender_2
endmodule
