// Logisim project CUPU - Kopie.circ as structural Verilog: 17 circuits, main circuit main
module fpu (
  input  enable,
  input  [4:0] op,
  input  [31:0] a,
  input  [31:0] b,
  input  init,
  input  clk,
  output [31:0] result,
  output [7:0] flags,
  output rsm
);

  wire and_1_out, cordic_trig_1_resume, delay_1_out_2, fpnegator_1_p2, fpnegator_1_p3, fpnegator_1_p4,
       fpnegator_1_p5, inv_sqrt_1_inpt_zero, inv_sqrt_1_nan, ln_1_resume, nrt_1_out_6, potenz_float_1_resume,
       pull_resistor_1_node, sqrt_1_resume, undriven, undriven_2;
  wire [4:0] bit_extender_1_out, bit_extender_2_out;
  wire [7:0] multiplexer_3_out_2;
  wire [30:1] multiplexer_3_out;
  wire [31:0] cordic_trig_1_cos, cordic_trig_1_sin, cordic_trig_1_tan, fpadder_1_out, fpadder_2_out,
       fpdivider_1_out, fpmultiplier_1_out, fpnegator_1_p6, fpsubtractor_1_out, fpsubtractor_2_out,
       inttofp_1_p2, inttofp_1_p3, inv_sqrt_1_aprox, ln_1_out_4, nrt_1_out_5, potenz_float_1_res,
       shifter_1_out, shifter_2_out, sqrt_1_res;

  Bit_Extender #(.in_width(32), .out_width(5)) bit_extender_1 (.in(b), .out(bit_extender_1_out));
  Bit_Extender #(.in_width(32), .out_width(5)) bit_extender_2 (.in(b), .out(bit_extender_2_out));
  // Random #(.width(32)) random_1: pin names not known; wires that end beside it: 1'b1, enable
  Pull_Resistor pull_resistor_1 (.node(pull_resistor_1_node));
  assign pull_resistor_1_node = enable ? clk : 1'bz;  // Controlled_Buffer controlled_buffer_1
  FPAdder fpadder_1 (.a(a), .b(b), .out(fpadder_1_out));
  FPSubtractor fpsubtractor_1 (.a(a), .b(b), .out(fpsubtractor_1_out));
  FPMultiplier fpmultiplier_1 (.a(a), .b(b), .out(fpmultiplier_1_out));
  FPDivider fpdivider_1 (.a(a), .b(b), .out(fpdivider_1_out));
  FPAdder fpadder_2 (.a(a), .b(32'h1), .out(fpadder_2_out));
  FPSubtractor fpsubtractor_2 (.a(a), .b(32'h1), .out(fpsubtractor_2_out));
  // FPNegator fpnegator_1: pin names not known; wires that end beside it: a, fpnegator_1_p2, fpnegator_1_p3, fpnegator_1_p4, fpnegator_1_p5, fpnegator_1_p6
  Shifter #(.width(32)) shifter_1 (.in(a), .\dist (bit_extender_1_out), .out(shifter_1_out));
  Shifter #(.shift("lr"), .width(32)) shifter_2 (.in(a), .\dist (bit_extender_2_out), .out(shifter_2_out));
  // IntToFP #(.width(32)) inttofp_1: pin names not known; wires that end beside it: a, inttofp_1_p2, inttofp_1_p3
  inv_sqrt inv_sqrt_1 (.in_1(a), .aprox(inv_sqrt_1_aprox), .NaN(inv_sqrt_1_nan), .inpt_zero(inv_sqrt_1_inpt_zero));
  cordic_trig cordic_trig_1 (
    .ang(a), .reset(init), .takt(pull_resistor_1_node), .cos(cordic_trig_1_cos), .sin(cordic_trig_1_sin),
    .tan(cordic_trig_1_tan), .resume(cordic_trig_1_resume));
  sqrt sqrt_1 (.root(a), .reset(init), .takt(pull_resistor_1_node), .res(sqrt_1_res), .resume(sqrt_1_resume));
  potenz_float potenz_float_1 (
    .inpt(a), .power(b), .reset(init), .takt(pull_resistor_1_node), .res(potenz_float_1_res),
    .resume(potenz_float_1_resume));
  nrt nrt_1 (.x(a), .deg(b), .in_3(init), .in_4(pull_resistor_1_node), .out_5(nrt_1_out_5), .out_6(nrt_1_out_6));
  ln ln_1 (.x(a), .reset(init), .clk(pull_resistor_1_node), .out_4(ln_1_out_4), .resume(ln_1_resume));
  Pull_Resistor pull_resistor_2 (.node(multiplexer_3_out_2[3]));
  Multiplexer #(.select(5)) multiplexer_1 (
    .in0(undriven), .in1(undriven_2), .in2(fpnegator_1_p2), .in3(fpnegator_1_p3), .in4(fpnegator_1_p4),
    .in5(fpnegator_1_p5), .in6(inv_sqrt_1_nan), .in7(inv_sqrt_1_inpt_zero), .out(multiplexer_3_out_2[3]),
    .sel(op));  // open: in8, in9, in10, in11, in12, in13, in14, in15, in16, in17, in18, in19, in20, in21, in22, in23, in24, in25, in26, in27, in28, in29, in30, in31
  Multiplexer #(.select(5)) multiplexer_2 (
    .in0(1'b1), .in1(1'b1), .in2(1'b1), .in3(1'b1), .in4(1'b1), .in5(1'b1), .in6(1'b1), .in7(1'b1),
    .in8(1'b1), .in9(1'b1), .in10(1'b1), .in11(1'b1), .in12(cordic_trig_1_resume),
    .in13(cordic_trig_1_resume), .in14(cordic_trig_1_resume), .in15(sqrt_1_resume),
    .in16(potenz_float_1_resume), .in17(nrt_1_out_6), .in18(ln_1_resume), .in19(1'b1), .in20(1'b1),
    .in21(1'b1), .in22(1'b1), .in23(1'b1), .in24(1'b1), .in25(1'b1), .in26(1'b1), .in27(1'b1), .in28(1'b1),
    .in29(1'b1), .in30(1'b1), .in31(1'b1), .out(rsm), .sel(op));
  Multiplexer #(.select(5), .width(32)) multiplexer_3 (
    .in0(fpadder_1_out), .in1(fpsubtractor_1_out), .in2(fpmultiplier_1_out), .in3(fpdivider_1_out),
    .in4(fpadder_2_out), .in5(fpsubtractor_2_out), .in6(fpnegator_1_p6), .in7(shifter_1_out),
    .in8(shifter_2_out), .in9(inttofp_1_p2), .in10(inttofp_1_p3), .in11(inv_sqrt_1_aprox),
    .in12(cordic_trig_1_cos), .in13(cordic_trig_1_sin), .in14(cordic_trig_1_tan), .in15(sqrt_1_res),
    .in16(potenz_float_1_res), .in17(nrt_1_out_5), .in18(ln_1_out_4),
    .out({multiplexer_3_out_2[1], multiplexer_3_out, multiplexer_3_out_2[0]}), .sel(op));  // open: in19, in20, in21, in22, in23, in24, in25, in26, in27, in28, in29, in30, in31
  // FPComparator fpcomparator_1: pin names not known; wires that end beside it: {multiplexer_3_out_2[1], multiplexer_3_out, multiplexer_3_out_2[0]}, {32{1'b0}}, multiplexer_3_out_2[2]
  // FPComparator fpcomparator_2: pin names not known; wires that end beside it: {multiplexer_3_out_2[1], multiplexer_3_out, multiplexer_3_out_2[0]}, {32{1'b1}}, multiplexer_3_out_2[4]
  // FPComparator fpcomparator_3: pin names not known; wires that end beside it: a, b, multiplexer_3_out_2[5], multiplexer_3_out_2[6], multiplexer_3_out_2[7]
  and and_1 (and_1_out, enable, rsm);
  Register register_1 (.D(multiplexer_3_out_2), .Q(flags), .clk(delay_1_out_2));  // open: en, clr
  delay delay_1 (.in_1(and_1_out), .out_2(delay_1_out_2));
  // Probe on result
  Register #(.width(32)) register_2 (
    .D({multiplexer_3_out_2[1], multiplexer_3_out, multiplexer_3_out_2[0]}), .Q(result), .clk(delay_1_out_2));  // open: en, clr
endmodule

module alu (
  input  enable,
  input  [4:0] op,
  input  [31:0] a,
  input  [31:0] b,
  input  init,
  input  clk,
  output [31:0] result,
  output [7:0] flags,
  output rsm
);

  wire adder_1_cout, adder_2_cout, and_2_out, delay_1_out_2, multiplexer_3_out, potenz_int_1_resume,
       pull_resistor_1_node, subtractor_1_bout, subtractor_2_bout;
  wire [4:0] bit_extender_1_out, bit_extender_2_out;
  wire [7:0] multiplexer_1_out_2;
  wire [30:1] multiplexer_1_out;
  wire [31:0] adder_1_out, adder_2_out, and_1_out, divider_1_out, divider_1_rem, fptoint_1_p3, fptoint_1_p4,
       multiplier_1_cout, multiplier_1_out, nand_1_out, negator_1_out, nor_1_out, not_1_out, or_1_out,
       potenz_int_1_res, shifter_1_out, shifter_2_out, subtractor_1_out, subtractor_2_out, xnor_1_out,
       xor_1_out;

  Bit_Extender #(.in_width(32), .out_width(5)) bit_extender_1 (.in(b), .out(bit_extender_1_out));
  Bit_Extender #(.in_width(32), .out_width(5)) bit_extender_2 (.in(b), .out(bit_extender_2_out));
  Random #(.width(32)) random_1 ();  // open: clk, next, out, clr
  Pull_Resistor pull_resistor_1 (.node(pull_resistor_1_node));
  assign pull_resistor_1_node = enable ? clk : 1'bz;  // Controlled_Buffer controlled_buffer_1
  Adder #(.width(32)) adder_1 (.a(a), .b(b), .out(adder_1_out), .cout(adder_1_cout));  // open: cin
  Subtractor #(.width(32)) subtractor_1 (.a(a), .b(b), .out(subtractor_1_out), .bout(subtractor_1_bout));  // open: bin
  Multiplier #(.width(32)) multiplier_1 (.a(a), .b(b), .out(multiplier_1_out), .cout(multiplier_1_cout));  // open: cin
  Divider #(.width(32)) divider_1 (.a(a), .b(b), .out(divider_1_out), .rem(divider_1_rem));  // open: upper
  Adder #(.width(32)) adder_2 (.a(a), .b(32'h1), .out(adder_2_out), .cout(adder_2_cout));  // open: cin
  Subtractor #(.width(32)) subtractor_2 (
    .a(a), .b(32'h1), .out(subtractor_2_out), .bout(subtractor_2_bout));  // open: bin
  Negator #(.width(32)) negator_1 (.in(a), .out(negator_1_out));
  Shifter #(.width(32)) shifter_1 (.in(a), .\dist (bit_extender_1_out), .out(shifter_1_out));
  Shifter #(.shift("lr"), .width(32)) shifter_2 (.in(a), .\dist (bit_extender_2_out), .out(shifter_2_out));
  assign or_1_out = a | b;  // OR_Gate or_1, 32 bits wide
  assign and_1_out = a & b;  // AND_Gate and_1, 32 bits wide
  assign xor_1_out = a ^ b;  // XOR_Gate xor_1, 32 bits wide
  assign not_1_out = ~a;  // NOT_Gate not_1, 32 bits wide
  assign nor_1_out = ~(a | b);  // NOR_Gate nor_1, 32 bits wide
  assign nand_1_out = ~(a & b);  // NAND_Gate nand_1, 32 bits wide
  assign xnor_1_out = ~(a ^ b);  // XNOR_Gate xnor_1, 32 bits wide
  // FPToInt #(.width(32)) fptoint_1: pin names not known; wires that end beside it: a, enable, fptoint_1_p3, fptoint_1_p4
  potenz_int potenz_int_1 (
    .inpt(a), .power(b), .reset(init), .takt(pull_resistor_1_node), .res(potenz_int_1_res),
    .resume(potenz_int_1_resume));
  Multiplexer #(.select(5), .width(32)) multiplexer_1 (
    .in0(adder_1_out), .in1(subtractor_1_out), .in2(multiplier_1_out), .in3(divider_1_out),
    .in4(adder_2_out), .in5(subtractor_2_out), .in6(negator_1_out), .in7(shifter_1_out), .in8(shifter_2_out),
    .in9(or_1_out), .in10(and_1_out), .in11(xor_1_out), .in12(not_1_out), .in13(nor_1_out),
    .in14(nand_1_out), .in15(xnor_1_out), .in16(fptoint_1_p3), .in17(fptoint_1_p4), .in19(multiplier_1_cout),
    .in20(divider_1_rem), .in21(potenz_int_1_res), .in31(a),
    .out({multiplexer_1_out_2[1], multiplexer_1_out, multiplexer_1_out_2[0]}), .sel(op));  // open: in18, in22, in23, in24, in25, in26, in27, in28, in29, in30
  Multiplexer #(.select(5)) multiplexer_2 (
    .in0(adder_1_cout), .in1(subtractor_1_bout), .in4(adder_2_cout), .in5(subtractor_2_bout),
    .out(multiplexer_1_out_2[3]), .sel(op));  // open: in2, in3, in6, in7, in8, in9, in10, in11, in12, in13, in14, in15, in16, in17, in18, in19, in20, in21, in22, in23, in24, in25, in26, in27, in28, in29, in30, in31
  Multiplexer #(.select(5)) multiplexer_3 (
    .in0(1'b1), .in1(1'b1), .in2(1'b1), .in3(1'b1), .in4(1'b1), .in5(1'b1), .in6(1'b1), .in7(1'b1),
    .in8(1'b1), .in9(1'b1), .in10(1'b1), .in11(1'b1), .in12(1'b1), .in13(1'b1), .in14(1'b1), .in15(1'b1),
    .in16(1'b1), .in17(1'b1), .in18(1'b1), .in19(1'b1), .in20(1'b1), .in21(potenz_int_1_resume), .in22(1'b1),
    .in23(1'b1), .in24(1'b1), .in25(1'b1), .in26(1'b1), .in27(1'b1), .in28(1'b1), .in29(1'b1), .in30(1'b1),
    .in31(1'b1), .out(multiplexer_3_out), .sel(op));
  and and_2 (and_2_out, enable, multiplexer_3_out);
  Comparator #(.width(32)) comparator_1 (
    .a({multiplexer_1_out_2[1], multiplexer_1_out, multiplexer_1_out_2[0]}), .b({32{1'b0}}),
    .eq(multiplexer_1_out_2[2]));  // open: gt, lt
  Comparator #(.width(32)) comparator_2 (
    .a({multiplexer_1_out_2[1], multiplexer_1_out, multiplexer_1_out_2[0]}), .b({32{1'b1}}),
    .eq(multiplexer_1_out_2[4]));  // open: gt, lt
  Comparator #(.width(32)) comparator_3 (
    .a(a), .b(b), .gt(multiplexer_1_out_2[5]), .eq(multiplexer_1_out_2[6]), .lt(multiplexer_1_out_2[7]));
  Pull_Resistor pull_resistor_2 (.node(multiplexer_1_out_2));
  delay delay_1 (.in_1(multiplexer_3_out), .out_2(delay_1_out_2));
  Register #(.width(32)) register_1 (
    .D({multiplexer_1_out_2[1], multiplexer_1_out, multiplexer_1_out_2[0]}), .Q(result), .clk(and_2_out));  // open: en, clr
  Register register_2 (.D(multiplexer_1_out_2), .Q(flags), .clk(and_2_out));  // open: en, clr
  delay delay_2 (.in_1(delay_1_out_2), .out_2(rsm));
endmodule

module regs (
  input  [7:0] s0_sel,
  input  [7:0] s1_sel,
  input  [7:0] dest_sel,
  input  [31:0] data,
  input  load,
  output [31:0] out_6,
  output [31:0] out_7
);

  wire decoder_1_out0, decoder_1_out1, decoder_1_out2, decoder_1_out3, decoder_1_out4, decoder_1_out5,
       decoder_1_out6, decoder_1_out7, decoder_1_out8, decoder_1_out9, decoder_1_out10, decoder_1_out11,
       decoder_1_out12, decoder_1_out13, decoder_1_out14, decoder_1_out15, delay_1_out_2;
  wire [3:0] bit_extender_1_out, bit_extender_2_out, bit_extender_3_out;
  wire [31:0] fp_q, ra_q, register_1_q, register_2_q, register_3_q, register_4_q, register_5_q, register_6_q,
       register_7_q, register_8_q, register_9_q, register_10_q, register_11_q, register_12_q, register_13_q,
       sp_q;

  Bit_Extender #(.out_width(4)) bit_extender_1 (.in(s0_sel), .out(bit_extender_1_out));
  Bit_Extender #(.out_width(4)) bit_extender_2 (.in(s1_sel), .out(bit_extender_2_out));
  Bit_Extender #(.out_width(4)) bit_extender_3 (.in(dest_sel), .out(bit_extender_3_out));
  Decoder #(.select(4)) decoder_1 (
    .out0(decoder_1_out0), .out1(decoder_1_out1), .out2(decoder_1_out2), .out3(decoder_1_out3),
    .out4(decoder_1_out4), .out5(decoder_1_out5), .out6(decoder_1_out6), .out7(decoder_1_out7),
    .out8(decoder_1_out8), .out9(decoder_1_out9), .out10(decoder_1_out10), .out11(decoder_1_out11),
    .out12(decoder_1_out12), .out13(decoder_1_out13), .out14(decoder_1_out14), .out15(decoder_1_out15),
    .sel(bit_extender_3_out), .en(delay_1_out_2));
  delay delay_1 (.in_1(load), .out_2(delay_1_out_2));
  Register #(.width(32)) register_1 (.D(data), .Q(register_1_q), .clk(decoder_1_out0));  // open: en, clr
  Register #(.width(32)) register_2 (.D(data), .Q(register_2_q), .clk(decoder_1_out1));  // open: en, clr
  Register #(.width(32)) register_3 (.D(data), .Q(register_3_q), .clk(decoder_1_out2));  // open: en, clr
  Register #(.width(32)) register_4 (.D(data), .Q(register_4_q), .clk(decoder_1_out3));  // open: en, clr
  Register #(.width(32)) register_5 (.D(data), .Q(register_5_q), .clk(decoder_1_out4));  // open: en, clr
  Register #(.width(32)) register_6 (.D(data), .Q(register_6_q), .clk(decoder_1_out5));  // open: en, clr
  Register #(.width(32)) register_7 (.D(data), .Q(register_7_q), .clk(decoder_1_out6));  // open: en, clr
  Register #(.width(32)) register_8 (.D(data), .Q(register_8_q), .clk(decoder_1_out7));  // open: en, clr
  Register #(.width(32)) register_9 (.D(data), .Q(register_9_q), .clk(decoder_1_out8));  // open: en, clr
  Register #(.width(32)) register_10 (.D(data), .Q(register_10_q), .clk(decoder_1_out9));  // open: en, clr
  Register #(.width(32)) register_11 (.D(data), .Q(register_11_q), .clk(decoder_1_out10));  // open: en, clr
  Register #(.width(32)) register_12 (.D(data), .Q(register_12_q), .clk(decoder_1_out11));  // open: en, clr
  Register #(.width(32)) register_13 (.D(data), .Q(register_13_q), .clk(decoder_1_out12));  // open: en, clr
  Register #(.width(32)) sp (.D(data), .Q(sp_q), .clk(decoder_1_out13));  // open: en, clr
  Register #(.width(32)) fp (.D(data), .Q(fp_q), .clk(decoder_1_out14));  // open: en, clr
  Register #(.width(32)) ra (.D(data), .Q(ra_q), .clk(decoder_1_out15));  // open: en, clr
  Multiplexer #(.select(4), .width(32)) multiplexer_1 (
    .in0(register_1_q), .in1(register_2_q), .in2(register_3_q), .in3(register_4_q), .in4(register_5_q),
    .in5(register_6_q), .in6(register_7_q), .in7(register_8_q), .in8(register_9_q), .in9(register_10_q),
    .in10(register_11_q), .in11(register_12_q), .in12(register_13_q), .in13(sp_q), .in14(fp_q), .in15(ra_q),
    .out(out_6), .sel(bit_extender_1_out));
  Multiplexer #(.select(4), .width(32)) multiplexer_2 (
    .in0(register_1_q), .in1(register_2_q), .in2(register_3_q), .in3(register_4_q), .in4(register_5_q),
    .in5(register_6_q), .in6(register_7_q), .in7(register_8_q), .in8(register_9_q), .in9(register_10_q),
    .in10(register_11_q), .in11(register_12_q), .in12(register_13_q), .in13(sp_q), .in14(fp_q), .in15(ra_q),
    .out(out_7), .sel(bit_extender_2_out));
endmodule

module delay (
  input  in_1,
  output out_2
);

  wire buffer_1_out, buffer_2_out, buffer_3_out, buffer_4_out, buffer_5_out, buffer_6_out, buffer_7_out,
       buffer_8_out, buffer_9_out, buffer_10_out, buffer_11_out, buffer_12_out, buffer_13_out, buffer_14_out,
       buffer_15_out, buffer_16_out, buffer_17_out, buffer_18_out, buffer_19_out, buffer_20_out,
       buffer_21_out, buffer_22_out, buffer_23_out, buffer_24_out, buffer_25_out, buffer_26_out,
       buffer_27_out, buffer_28_out, buffer_29_out, buffer_30_out, buffer_31_out, buffer_32_out,
       buffer_33_out, buffer_34_out, buffer_35_out, buffer_36_out, buffer_37_out, buffer_38_out,
       buffer_39_out, buffer_40_out, buffer_41_out, buffer_42_out, buffer_43_out, buffer_44_out,
       buffer_45_out, buffer_46_out, buffer_47_out;

  buf buffer_1 (buffer_1_out, in_1);
  buf buffer_2 (buffer_2_out, buffer_1_out);
  buf buffer_3 (buffer_3_out, buffer_2_out);
  buf buffer_4 (buffer_4_out, buffer_5_out);
  buf buffer_5 (buffer_5_out, buffer_6_out);
  buf buffer_6 (buffer_6_out, buffer_7_out);
  buf buffer_7 (buffer_7_out, buffer_15_out);
  buf buffer_8 (buffer_8_out, buffer_4_out);
  buf buffer_9 (buffer_9_out, buffer_8_out);
  buf buffer_10 (buffer_10_out, buffer_9_out);
  buf buffer_11 (buffer_11_out, buffer_3_out);
  buf buffer_12 (buffer_12_out, buffer_11_out);
  buf buffer_13 (buffer_13_out, buffer_12_out);
  buf buffer_14 (buffer_14_out, buffer_13_out);
  buf buffer_15 (buffer_15_out, buffer_16_out);
  buf buffer_16 (buffer_16_out, buffer_17_out);
  buf buffer_17 (buffer_17_out, buffer_18_out);
  buf buffer_18 (buffer_18_out, buffer_27_out);
  buf buffer_19 (buffer_19_out, buffer_10_out);
  buf buffer_20 (buffer_20_out, buffer_19_out);
  buf buffer_21 (buffer_21_out, buffer_20_out);
  buf buffer_22 (buffer_22_out, buffer_21_out);
  buf buffer_23 (buffer_23_out, buffer_14_out);
  buf buffer_24 (buffer_24_out, buffer_23_out);
  buf buffer_25 (buffer_25_out, buffer_24_out);
  buf buffer_26 (buffer_26_out, buffer_25_out);
  buf buffer_27 (buffer_27_out, buffer_28_out);
  buf buffer_28 (buffer_28_out, buffer_29_out);
  buf buffer_29 (buffer_29_out, buffer_30_out);
  buf buffer_30 (buffer_30_out, buffer_39_out);
  buf buffer_31 (buffer_31_out, buffer_22_out);
  buf buffer_32 (buffer_32_out, buffer_31_out);
  buf buffer_33 (buffer_33_out, buffer_32_out);
  buf buffer_34 (buffer_34_out, buffer_33_out);
  buf buffer_35 (buffer_35_out, buffer_26_out);
  buf buffer_36 (buffer_36_out, buffer_35_out);
  buf buffer_37 (buffer_37_out, buffer_36_out);
  buf buffer_38 (buffer_38_out, buffer_37_out);
  buf buffer_39 (buffer_39_out, buffer_40_out);
  buf buffer_40 (buffer_40_out, buffer_41_out);
  buf buffer_41 (buffer_41_out, buffer_42_out);
  buf buffer_42 (buffer_42_out, buffer_47_out);
  buf buffer_43 (buffer_43_out, buffer_34_out);
  buf buffer_44 (buffer_44_out, buffer_43_out);
  buf buffer_45 (buffer_45_out, buffer_44_out);
  buf buffer_46 (buffer_46_out, buffer_45_out);
  buf buffer_47 (buffer_47_out, buffer_38_out);
  buf buffer_48 (out_2, buffer_46_out);
endmodule

module inv_sqrt (
  input  [31:0] in_1,
  output [31:0] aprox,
  output NaN,
  output inpt_zero
);

  wire [31:0] fpmultiplier_1_out, inv_sqrt_raphson_1_improved, shifter_1_out, subtractor_1_out;

  Shifter #(.shift("lr"), .width(32)) shifter_1 (.in(in_1), .\dist (5'b00001), .out(shifter_1_out));
  FPMultiplier fpmultiplier_1 (.a(in_1), .b(32'h3f000000), .out(fpmultiplier_1_out));
  // FPComparator fpcomparator_1: pin names not known; wires that end beside it: in_1, {32{1'b0}}, NaN, inpt_zero
  Subtractor #(.width(32)) subtractor_1 (
    .a(32'h5f3759df), .b(shifter_1_out), .out(subtractor_1_out));  // open: bin, bout
  inv_sqrt_raphson inv_sqrt_raphson_1 (
    .x(subtractor_1_out), .half_initial(fpmultiplier_1_out), .improved(inv_sqrt_raphson_1_improved));
  inv_sqrt_raphson inv_sqrt_raphson_2 (
    .x(inv_sqrt_raphson_1_improved), .half_initial(fpmultiplier_1_out), .improved(aprox));
endmodule

module inv_sqrt_raphson (
  input  [31:0] x,
  input  [31:0] half_initial,
  output [31:0] improved
);

  wire [31:0] fpmultiplier_1_out, fpmultiplier_2_out, fpsubtractor_1_out;

  FPMultiplier fpmultiplier_1 (.a(x), .b(x), .out(fpmultiplier_1_out));
  FPMultiplier fpmultiplier_2 (.a(fpmultiplier_1_out), .b(half_initial), .out(fpmultiplier_2_out));
  FPSubtractor fpsubtractor_1 (.a(32'h3fc00000), .b(fpmultiplier_2_out), .out(fpsubtractor_1_out));
  FPMultiplier fpmultiplier_3 (.a(x), .b(fpsubtractor_1_out), .out(improved));
endmodule

module cordic_trig (
  input  [31:0] ang,
  input  reset,
  input  takt,
  output [31:0] cos,
  output [31:0] sin,
  output [31:0] tan,
  output resume
);

  wire delay_1_out_2, delay_2_out_2, delay_3_out_2, fpcomparator_1_p3, fpcomparator_1_p4, or_1_out, or_2_out,
       or_3_out;
  wire [4:0] i_q;
  wire [31:0] fpadder_1_out, fpdivider_1_out, fpdivider_2_out, fpnegator_1_p2, fpnegator_2_p2,
       fpnegator_3_p2, fpsubtractor_1_out, fpsubtractor_2_out, inttofp_1_p2, multiplexer_1_out,
       multiplexer_2_out, multiplexer_3_out, multiplexer_4_out, multiplexer_5_out, rom_1_data, shifter_1_out,
       z_q;

  delay delay_1 (.in_1(takt), .out_2(delay_1_out_2));
  Multiplexer #(.width(32)) multiplexer_1 (
    .in0(fpsubtractor_1_out), .in1(32'h3f1b74ee), .out(multiplexer_1_out), .sel(reset));
  Register #(.width(32)) x (.D(multiplexer_1_out), .Q(cos), .clk(or_1_out));  // open: en, clr
  or or_1 (or_1_out, delay_2_out_2, takt);
  delay delay_2 (.in_1(reset), .out_2(delay_2_out_2));
  Register #(.width(32)) y (.D(fpadder_1_out), .Q(sin), .clk(takt), .clr(reset));  // open: en
  Multiplexer #(.width(32)) multiplexer_2 (.in0(fpsubtractor_2_out), .in1(ang), .out(multiplexer_2_out), .sel(reset));
  Register #(.width(32)) z (.D(multiplexer_2_out), .Q(z_q), .clk(or_2_out));  // open: en, clr
  or or_2 (or_2_out, delay_3_out_2, takt);
  delay delay_3 (.in_1(reset), .out_2(delay_3_out_2));
  Counter #(.max('h1f), .width(5)) i (.Q(i_q), .carry(resume), .clk(delay_1_out_2));  // open: load, D, count, up, clr
  ROM #(.addrWidth(5), .dataWidth(32)) rom_1 (.addr(i_q), .data(rom_1_data));
  Shifter #(.width(32)) shifter_1 (.in(32'h1), .\dist (i_q), .out(shifter_1_out));
  // FPComparator fpcomparator_1: pin names not known; wires that end beside it: z_q, {32{1'b0}}, fpcomparator_1_p3, fpcomparator_1_p4
  // IntToFP #(.mode("unsigned"), .width(32)) inttofp_1: pin names not known; wires that end beside it: shifter_1_out, inttofp_1_p2
  or or_3 (or_3_out, fpcomparator_1_p3, fpcomparator_1_p4);
  FPDivider fpdivider_1 (.a(cos), .b(inttofp_1_p2), .out(fpdivider_1_out));
  // FPNegator fpnegator_1: pin names not known; wires that end beside it: fpdivider_1_out, fpnegator_1_p2
  FPDivider fpdivider_2 (.a(sin), .b(inttofp_1_p2), .out(fpdivider_2_out));
  // FPNegator fpnegator_2: pin names not known; wires that end beside it: fpdivider_2_out, fpnegator_2_p2
  // FPNegator fpnegator_3: pin names not known; wires that end beside it: rom_1_data, fpnegator_3_p2
  Multiplexer #(.width(32)) multiplexer_3 (
    .in0(fpnegator_1_p2), .in1(fpdivider_1_out), .out(multiplexer_3_out), .sel(or_3_out));
  Multiplexer #(.width(32)) multiplexer_4 (
    .in0(fpnegator_2_p2), .in1(fpdivider_2_out), .out(multiplexer_4_out), .sel(or_3_out));
  Multiplexer #(.width(32)) multiplexer_5 (
    .in0(fpnegator_3_p2), .in1(rom_1_data), .out(multiplexer_5_out), .sel(or_3_out));
  FPAdder fpadder_1 (.a(sin), .b(multiplexer_3_out), .out(fpadder_1_out));
  FPSubtractor fpsubtractor_1 (.a(cos), .b(multiplexer_4_out), .out(fpsubtractor_1_out));
  FPSubtractor fpsubtractor_2 (.a(z_q), .b(multiplexer_5_out), .out(fpsubtractor_2_out));
  FPDivider fpdivider_3 (.a(sin), .b(cos), .out(tan));

  // Notes on the sheet:
  //   contents of rom_1 (hex, n*v repeats v):
  //   3f490fdb 3eed6338 3e7adbb0 3dfeadd5 3d7faade 3cffeaae 3c7ffaab 3bfffeab 3b7fffab 3affffeb 3a7ffffb
  //   39ffffff 39800000 39000000 38800000 38000000 37800000 37000000 36800000 36000000 35800000 35000000
  //   34800000 34000000 33800000 33000000 32800000 32000000 31800000 31000000 30800000 30000000
endmodule

module sqrt (
  input  [31:0] root,
  input  reset,
  input  takt,
  output [31:0] res,
  output resume
);

  wire comparator_1_gt;
  wire [31:0] counter_1_q, fpadder_1_out, fpdivider_1_out, multiplexer_1_out, x_n_q;

  Multiplexer #(.width(32)) multiplexer_1 (.in0(root), .in1(res), .out(multiplexer_1_out), .sel(comparator_1_gt));
  Counter #(.max('h6), .width(32)) counter_1 (
    .Q(counter_1_q), .carry(resume), .clk(takt), .clr(reset));  // open: load, D, count, up
  Register #(.width(32)) x_n (.D(multiplexer_1_out), .Q(x_n_q), .clk(takt), .clr(reset));  // open: en
  Comparator #(.mode("unsigned"), .width(32)) comparator_1 (
    .a(counter_1_q), .b({32{1'b0}}), .gt(comparator_1_gt));  // open: eq, lt
  FPDivider fpdivider_1 (.a(root), .b(x_n_q), .out(fpdivider_1_out));
  FPAdder fpadder_1 (.a(fpdivider_1_out), .b(x_n_q), .out(fpadder_1_out));
  FPMultiplier fpmultiplier_1 (.a(fpadder_1_out), .b(32'h3f000000), .out(res));
  // Probe on res
endmodule

module potenz_float (
  input  [31:0] inpt,
  input  [31:0] power,
  input  reset,
  input  takt,
  output [31:0] res,
  output resume
);

  wire and_1_out, delay_1_out_2, delay_2_out_2, fpcomparator_1_p3, fpcomparator_2_p3, inttofp_1_p2, or_1_out;
  wire [31:0] counter_1_q, fpmultiplier_1_out, fpsubtractor_1_out, multiplexer_1_out, register_1_q,
       register_2_q, register_3_q;

  Register #(.width(32)) register_1 (.D(inpt), .Q(register_1_q), .clk(reset));  // open: en, clr
  Register #(.width(32)) register_2 (.D(power), .Q(register_2_q), .clk(reset));  // open: en, clr
  // FPComparator fpcomparator_1: pin names not known; wires that end beside it: register_2_q, 32'h3f800000, fpcomparator_1_p3
  Multiplexer #(.width(32)) multiplexer_1 (
    .in0(fpmultiplier_1_out), .in1(register_1_q), .out(multiplexer_1_out), .sel(reset));
  Register #(.width(32)) register_3 (.D(multiplexer_1_out), .Q(register_3_q), .clk(or_1_out));  // open: en, clr
  or or_1 (or_1_out, delay_1_out_2, and_1_out);
  delay delay_1 (.in_1(reset), .out_2(delay_1_out_2));
  Counter #(.max('hffffffff), .width(32)) counter_1 (
    .Q(counter_1_q), .clk(and_1_out), .clr(reset));  // open: load, D, count, carry, up
  and and_1 (and_1_out, takt, ~fpcomparator_2_p3);  // AND_Gate
  // IntToFP #(.mode("unsigned"), .width(32)) inttofp_1: pin names not known; wires that end beside it: counter_1_q, inttofp_1_p2
  FPMultiplier fpmultiplier_1 (.a(register_3_q), .b(register_1_q), .out(fpmultiplier_1_out));
  FPSubtractor fpsubtractor_1 (.a(register_2_q), .b(32'h3f800000), .out(fpsubtractor_1_out));
  // FPComparator fpcomparator_2: pin names not known; wires that end beside it: fpsubtractor_1_out, inttofp_1_p2, fpcomparator_2_p3
  Multiplexer #(.width(32)) multiplexer_2 (.in0(register_3_q), .in1(register_1_q), .out(res), .sel(fpcomparator_1_p3));
  delay delay_2 (.in_1(fpcomparator_1_p3), .out_2(delay_2_out_2));
  or or_2 (resume, delay_2_out_2, fpcomparator_2_p3);
endmodule

module potenz_int (
  input  [31:0] inpt,
  input  [31:0] power,
  input  reset,
  input  takt,
  output [31:0] res,
  output resume
);

  wire and_1_out, comparator_1_eq, comparator_2_eq, delay_1_out_2, delay_2_out_2, or_1_out;
  wire [31:0] counter_1_q, multiplexer_1_out, multiplier_1_out, register_1_q, subtractor_1_out;

  Comparator #(.width(32)) comparator_1 (.a(power), .b(32'h1), .eq(comparator_1_eq));  // open: gt, lt
  Multiplexer #(.width(32)) multiplexer_1 (.in0(multiplier_1_out), .in1(inpt), .out(multiplexer_1_out), .sel(reset));
  Register #(.width(32)) register_1 (.D(multiplexer_1_out), .Q(register_1_q), .clk(or_1_out));  // open: en, clr
  or or_1 (or_1_out, delay_1_out_2, and_1_out);
  delay delay_1 (.in_1(reset), .out_2(delay_1_out_2));
  Counter #(.max('hffffffff), .trigger("falling"), .width(32)) counter_1 (
    .Q(counter_1_q), .clk(and_1_out), .clr(reset));  // open: load, D, count, carry, up
  and and_1 (and_1_out, takt, ~comparator_2_eq);  // AND_Gate
  Multiplier #(.width(32)) multiplier_1 (.a(register_1_q), .b(inpt), .out(multiplier_1_out));  // open: cin, cout
  Subtractor #(.width(32)) subtractor_1 (.a(power), .b(32'h1), .out(subtractor_1_out));  // open: bin, bout
  Comparator #(.width(32)) comparator_2 (.a(subtractor_1_out), .b(counter_1_q), .eq(comparator_2_eq));  // open: gt, lt
  Multiplexer #(.width(32)) multiplexer_2 (.in0(register_1_q), .in1(inpt), .out(res), .sel(comparator_1_eq));
  delay delay_2 (.in_1(comparator_1_eq), .out_2(delay_2_out_2));
  or or_2 (resume, delay_2_out_2, comparator_2_eq);
endmodule

module nrt (
  input  [31:0] x,
  input  [31:0] deg,
  input  in_3,
  input  in_4,
  output [31:0] out_5,
  output out_6
);

  wire and_1_out, and_2_out, delay_1_out_2, delay_2_out_2, delay_3_out_2, delay_4_out_2, delay_5_out_2,
       delay_6_out_2, delay_7_out_2, delay_8_out_2, fpcomparator_1_p3, fpcomparator_2_p3, fpcomparator_3_p3,
       fpcomparator_4_p3, not_1_out, not_2_out, not_3_out, not_4_out, or_1_out, or_2_out,
       potenz_float_1_resume, pull_resistor_1_node, pull_resistor_2_node, pull_resistor_3_node;
  wire [31:0] fpadder_1_out, fpdivider_1_out, fpdivider_2_out, fpsubtractor_1_out, fpsubtractor_2_out,
       multiplexer_1_out, multiplexer_2_out, multiplexer_3_out, potenz_float_1_res, register_1_q,
       register_2_q;

  not not_1 (not_1_out, out_6);
  Pull_Resistor pull_resistor_1 (.node(pull_resistor_1_node));
  assign pull_resistor_1_node = not_1_out ? in_4 : 1'bz;  // Controlled_Buffer controlled_buffer_1
  not not_2 (not_2_out, pull_resistor_1_node);
  delay delay_1 (.in_1(and_1_out), .out_2(delay_1_out_2));
  and and_1 (and_1_out, not_2_out, potenz_float_1_resume);
  delay delay_2 (.in_1(delay_1_out_2), .out_2(delay_2_out_2));
  delay delay_3 (.in_1(delay_2_out_2), .out_2(delay_3_out_2));
  not not_3 (not_3_out, out_6);
  Pull_Resistor pull_resistor_2 (.node(pull_resistor_2_node));
  assign pull_resistor_2_node = not_3_out ? delay_3_out_2 : 1'bz;  // Controlled_Buffer controlled_buffer_2
  or or_1 (or_1_out, pull_resistor_2_node, in_3);
  delay delay_4 (.in_1(or_1_out), .out_2(delay_4_out_2));
  FPDivider fpdivider_1 (.a(x), .b(32'h40000000), .out(fpdivider_1_out));
  potenz_float potenz_float_1 (
    .inpt(register_2_q), .power(deg), .reset(delay_5_out_2), .takt(pull_resistor_1_node),
    .res(potenz_float_1_res), .resume(potenz_float_1_resume));
  delay delay_5 (.in_1(delay_4_out_2), .out_2(delay_5_out_2));
  Multiplexer #(.width(32)) multiplexer_1 (
    .in0(fpdivider_2_out), .in1(fpdivider_1_out), .out(multiplexer_1_out), .sel(in_3));
  Multiplexer #(.width(32)) multiplexer_2 (
    .in0(multiplexer_3_out), .in1(fpdivider_1_out), .out(multiplexer_2_out), .sel(in_3));
  delay delay_6 (.in_1(or_2_out), .out_2(delay_6_out_2));
  Pull_Resistor pull_resistor_3 (.node(pull_resistor_3_node));
  assign pull_resistor_3_node = not_4_out ? potenz_float_1_resume : 1'bz;  // Controlled_Buffer controlled_buffer_3
  or or_2 (or_2_out, pull_resistor_3_node, in_3);
  not not_4 (not_4_out, delay_7_out_2);
  delay delay_7 (.in_1(delay_8_out_2), .out_2(delay_7_out_2));
  delay delay_8 (.in_1(out_6), .out_2(delay_8_out_2));
  Register #(.width(32)) register_1 (.D(multiplexer_1_out), .Q(register_1_q), .clk(delay_6_out_2));  // open: en, clr
  Register #(.width(32)) register_2 (.D(multiplexer_2_out), .Q(register_2_q), .clk(delay_6_out_2));  // open: en, clr
  Register #(.width(32)) register_3 (.D(register_2_q), .Q(out_5), .clk(out_6), .clr(in_3));  // open: en
  FPDivider fpdivider_2 (.a(register_1_q), .b(32'h40000000), .out(fpdivider_2_out));
  FPSubtractor fpsubtractor_1 (.a(register_2_q), .b(register_1_q), .out(fpsubtractor_1_out));
  Multiplexer #(.width(32)) multiplexer_3 (
    .in0(fpsubtractor_1_out), .in1(fpadder_1_out), .out(multiplexer_3_out), .sel(fpcomparator_1_p3));
  FPAdder fpadder_1 (.a(register_1_q), .b(register_2_q), .out(fpadder_1_out));
  // FPComparator fpcomparator_1: pin names not known; wires that end beside it: x, potenz_float_1_res, fpcomparator_1_p3
  FPSubtractor fpsubtractor_2 (.a(x), .b(potenz_float_1_res), .out(fpsubtractor_2_out));
  // FPComparator fpcomparator_2: pin names not known; wires that end beside it: register_1_q, {32{1'b0}}, fpcomparator_2_p3
  // FPComparator fpcomparator_3: pin names not known; wires that end beside it: fpsubtractor_2_out, 32'h3a03126f, fpcomparator_3_p3
  and and_2 (and_2_out, fpcomparator_3_p3, potenz_float_1_resume, fpcomparator_4_p3);
  // FPComparator fpcomparator_4: pin names not known; wires that end beside it: fpsubtractor_2_out, 32'hba03126f, fpcomparator_4_p3
  or or_3 (out_6, and_2_out, fpcomparator_2_p3);
endmodule

module ln (
  input  [31:0] x,
  input  reset,
  input  clk,
  output [31:0] out_4,
  output resume
);

  wire and_1_out, delay_1_out_2, delay_2_out_2, delay_3_out_2, delay_4_out_2, delay_5_out_2, delay_6_out_2,
       delay_7_out_2, delay_8_out_2, fpcomparator_1_p3, i_carry, not_1_out, or_1_out, or_2_out,
       pull_resistor_1_node, pull_resistor_2_node;
  wire [3:0] i_q;
  wire [31:0] fpadder_1_out, fpdivider_1_out, fpdivider_2_out, k_q, multiplexer_1_out, multiplexer_2_out,
       rom_1_data, z_q;

  Pull_Resistor pull_resistor_1 (.node(pull_resistor_1_node));
  assign pull_resistor_1_node = not_1_out ? clk : 1'bz;  // Controlled_Buffer controlled_buffer_1
  not not_1 (not_1_out, resume);
  Multiplexer #(.width(32)) multiplexer_1 (
    .in0(fpdivider_1_out), .in1(32'h3f800000), .out(multiplexer_1_out), .sel(reset));
  Register #(.width(32)) k (.D(multiplexer_1_out), .Q(k_q), .clk(or_1_out));  // open: en, clr
  or or_1 (or_1_out, delay_1_out_2, pull_resistor_2_node);
  delay delay_1 (.in_1(reset), .out_2(delay_1_out_2));
  Multiplexer #(.width(32)) multiplexer_2 (.in0(fpdivider_2_out), .in1(x), .out(multiplexer_2_out), .sel(reset));
  Register #(.width(32)) z (.D(multiplexer_2_out), .Q(z_q), .clk(or_2_out));  // open: en, clr
  or or_2 (or_2_out, delay_3_out_2, delay_2_out_2);
  delay delay_2 (.in_1(delay_4_out_2), .out_2(delay_2_out_2));
  delay delay_3 (.in_1(reset), .out_2(delay_3_out_2));
  delay delay_4 (.in_1(pull_resistor_1_node), .out_2(delay_4_out_2));
  Register #(.width(32)) ln_x (.D(fpadder_1_out), .Q(out_4), .clk(pull_resistor_1_node), .clr(reset));  // open: en
  Counter #(.max('hf), .trigger("falling"), .width(4)) i (
    .Q(i_q), .carry(i_carry), .clk(and_1_out), .clr(reset));  // open: load, D, count, up
  and and_1 (and_1_out, pull_resistor_1_node, delay_5_out_2);
  delay delay_5 (.in_1(delay_6_out_2), .out_2(delay_5_out_2));
  delay delay_6 (.in_1(fpcomparator_1_p3), .out_2(delay_6_out_2));
  and and_2 (resume, fpcomparator_1_p3, i_carry);
  FPDivider fpdivider_1 (.a(k_q), .b(32'h40000000), .out(fpdivider_1_out));
  FPDivider fpdivider_2 (.a(z_q), .b(rom_1_data), .out(fpdivider_2_out));
  FPAdder fpadder_1 (.a(out_4), .b(k_q), .out(fpadder_1_out));
  ROM #(.addrWidth(4), .dataWidth(32)) rom_1 (.addr(i_q), .data(rom_1_data));
  Pull_Resistor pull_resistor_2 (.node(pull_resistor_2_node));
  assign pull_resistor_2_node = delay_7_out_2 ? delay_4_out_2 : 1'bz;  // Controlled_Buffer controlled_buffer_2
  delay delay_7 (.in_1(delay_8_out_2), .out_2(delay_7_out_2));
  // FPComparator fpcomparator_1: pin names not known; wires that end beside it: fpdivider_2_out, rom_1_data, fpcomparator_1_p3
  delay delay_8 (.in_1(fpcomparator_1_p3), .out_2(delay_8_out_2));

  // Notes on the sheet:
  //   contents of rom_1 (hex, n*v repeats v):
  //   402df854 3fd3094c 3fa45af2 3f910b02 3f88415b 3f84102b 3f820405 3f810101 3f808040 3f804010 3f802004
  //   3f801001 3f800800 3f800400 3f800200 3f800100
endmodule

module main (
  input  [23:0] in_1,
  input  [31:0] in_2
);

  wire ram_1_p1;
  wire [7:0] ram_1_p13, ram_1_p14, ram_1_p15, ram_1_p16;

  // RAM #(.addrWidth(24), .enables("line"), .line("quad"), .misaligned("true"), .\type ("nonvolatile")) ram_1: pin names not known; wires that end beside it: ram_1_p1, in_1, 1'b1, 1'b1, 1'b1, 1'b0, 1'b1, ram_1_p1, in_2[7:0], in_2[15:8], in_2[23:16], in_2[31:24], ram_1_p13, ram_1_p14, ram_1_p15, ram_1_p16
  // Probe on {ram_1_p16, ram_1_p15, ram_1_p14, ram_1_p13}
endmodule

module cpu (
);

  wire alu_1_rsm, clock_1_out, clock_2_out, decoder_1_out1, decoder_1_out3, decoder_2_out1, decoder_2_out3,
       exec_1_enablecomp, exec_1_initcomp, exec_1_memread, exec_1_out_9, exec_1_out_10, fetch_1_out_13,
       fpu_1_rsm, multiplexer_5_out;
  wire [1:0] exec_1_memreadtype;
  wire [3:0] exec_1_out_16, exec_1_out_19, exec_1_out_20;
  wire [7:0] exec_1_out_11, exec_1_out_15, exec_1_out_17, exec_1_out_18, fetch_1_dregout,
       fetch_1_instextraout, fetch_1_instout, fetch_1_sreg0out, fetch_1_sreg1out, ram_1_p2, ram_1_p3,
       ram_1_p4, ram_1_p5;
  wire [23:0] fetch_1_out_6, memread_1_out_9, ram_1_p1;
  wire [31:0] alu_1_result, exec_1_immout, fetch_1_data, fpu_1_result, memread_1_data, multiplexer_2_out,
       multiplexer_3_out, multiplexer_4_out, regs_1_out_6, regs_1_out_7;

  // RAM #(.addrWidth(24), .enables("line"), .line("quad"), .misaligned("true"), .\type ("nonvolatile")) ram_1: pin names not known; wires that end beside it: ram_1_p1, ram_1_p2, ram_1_p3, ram_1_p4, ram_1_p5
  Multiplexer #(.width(24)) multiplexer_1 (
    .in0(memread_1_out_9), .in1(fetch_1_out_6), .out(ram_1_p1), .sel(clock_1_out));
  Clock clock_1 (.out(clock_1_out));
  memRead memread_1 (
    .out_9(memread_1_out_9), .in_4(ram_1_p2), .in_5(ram_1_p3), .in_6(ram_1_p4), .in_7(ram_1_p5),
    .address(multiplexer_4_out), .data(memread_1_data), .in_2(exec_1_memreadtype), .in_3(exec_1_memread));
  fetch fetch_1 (
    .out_6(fetch_1_out_6), .in_1(ram_1_p2), .in_2(ram_1_p3), .in_3(ram_1_p4), .in_4(ram_1_p5),
    .data(fetch_1_data), .instOut(fetch_1_instout), .instExtraOut(fetch_1_instextraout),
    .dRegOut(fetch_1_dregout), .sReg0Out(fetch_1_sreg0out), .sReg1Out(fetch_1_sreg1out), .in_5(exec_1_out_9),
    .out_13(fetch_1_out_13));
  exec exec_1 (
    .dataIn(fetch_1_data), .instIn(fetch_1_instout), .instExtraIn(fetch_1_instextraout),
    .dRegIn(fetch_1_dregout), .sReg0In(fetch_1_sreg0out), .sReg1In(fetch_1_sreg1out), .out_9(exec_1_out_9),
    .in_7(fetch_1_out_13), .out_10(exec_1_out_10), .out_11(exec_1_out_11), .memRead(exec_1_memread),
    .memReadType(exec_1_memreadtype), .immOut(exec_1_immout), .out_15(exec_1_out_15), .out_16(exec_1_out_16),
    .out_17(exec_1_out_17), .out_18(exec_1_out_18), .out_19(exec_1_out_19), .out_20(exec_1_out_20),
    .opRdy(multiplexer_5_out), .enableComp(exec_1_enablecomp), .initComp(exec_1_initcomp));
  regs regs_1 (
    .s0_sel(exec_1_out_18), .s1_sel(exec_1_out_17), .dest_sel(exec_1_out_11), .data(multiplexer_4_out),
    .load(exec_1_out_10), .out_6(regs_1_out_6), .out_7(regs_1_out_7));
  Multiplexer #(.select(4), .width(32)) multiplexer_2 (
    .in0(regs_1_out_6), .in1(exec_1_immout), .out(multiplexer_2_out), .sel(exec_1_out_20));  // open: in2, in3, in4, in5, in6, in7, in8, in9, in10, in11, in12, in13, in14, in15
  Multiplexer #(.select(4), .width(32)) multiplexer_3 (
    .in0(regs_1_out_7), .in1(exec_1_immout), .in2(regs_1_out_6), .out(multiplexer_3_out), .sel(exec_1_out_19));  // open: in3, in4, in5, in6, in7, in8, in9, in10, in11, in12, in13, in14, in15
  Decoder #(.select(4)) decoder_1 (
    .out1(decoder_1_out1), .out3(decoder_1_out3), .sel(exec_1_out_16), .en(exec_1_enablecomp));  // open: out0, out2, out4, out5, out6, out7, out8, out9, out10, out11, out12, out13, out14, out15
  Decoder #(.select(4)) decoder_2 (
    .out1(decoder_2_out1), .out3(decoder_2_out3), .sel(exec_1_out_16), .en(exec_1_initcomp));  // open: out0, out2, out4, out5, out6, out7, out8, out9, out10, out11, out12, out13, out14, out15
  alu alu_1 (
    .enable(decoder_1_out1), .op(exec_1_out_15[4:0]), .a(multiplexer_2_out), .b(multiplexer_3_out),
    .init(decoder_2_out1), .clk(clock_2_out), .result(alu_1_result), .rsm(alu_1_rsm));  // open: flags
  fpu fpu_1 (
    .enable(decoder_1_out3), .op(exec_1_out_15[4:0]), .a(multiplexer_2_out), .b(multiplexer_3_out),
    .init(decoder_2_out3), .clk(clock_2_out), .result(fpu_1_result), .rsm(fpu_1_rsm));  // open: flags
  Clock clock_2 (.out(clock_2_out));
  Multiplexer #(.select(4), .width(32)) multiplexer_4 (
    .in0(exec_1_immout), .in1(alu_1_result), .in3(fpu_1_result), .in5(regs_1_out_6), .in6(memread_1_data),
    .out(multiplexer_4_out), .sel(exec_1_out_16));  // open: in2, in4, in7, in8, in9, in10, in11, in12, in13, in14, in15
  Multiplexer #(.select(4)) multiplexer_5 (
    .in0(1'b1), .in1(alu_1_rsm), .in2(1'b1), .in3(fpu_1_rsm), .in4(1'b1), .out(multiplexer_5_out),
    .sel(exec_1_out_16));  // open: in5, in6, in7, in8, in9, in10, in11, in12, in13, in14, in15
endmodule

module fetch (
  input  [7:0] in_1,
  input  [7:0] in_2,
  input  [7:0] in_3,
  input  [7:0] in_4,
  input  in_5,
  output [23:0] out_6,
  output [31:0] data,
  output [7:0] instOut,
  output [7:0] instExtraOut,
  output [7:0] dRegOut,
  output [7:0] sReg0Out,
  output [7:0] sReg1Out,
  output out_13
);

  wire and_1_out, and_2_out, clock_1_out, delay_1_out_2, delay_2_out_2, delay_3_out_2, delay_4_out_2,
       delay_5_out_2, delay_6_out_2, delay_7_out_2, delay_8_out_2, delay_9_out_2, delay_10_out_2,
       delay_11_out_2, delay_12_out_2, delay_13_out_2, delay_14_out_2, delay_15_out_2, delay_16_out_2,
       delay_17_out_2, delay_18_out_2, delay_19_out_2, delay_20_out_2, delay_21_out_2, delay_22_out_2,
       delay_23_out_2, not_1_out, or_1_out, pull_resistor_1_node, pull_resistor_4_node;
  wire [0:0] or_2_out;
  wire [1:0] priority_encoder_1_out;
  wire [2:0] counter_1_q;
  wire [3:0] rom_1_data;
  wire [15:0] multiplexer_1_out, rom_2_data, rom_3_data, rom_4_data, rom_5_data, rom_6_data, rom_7_data,
       rom_8_data, rom_9_data, rom_10_data, rom_11_data, rom_12_data, rom_13_data, rom_14_data, rom_15_data,
       rom_16_data, rom_17_data;
  wire [30:0] pull_resistor_2_node;
  wire [31:0] adder_1_out, adder_2_out, bit_extender_1_out, multiplexer_2_out, multiplexer_3_out,
       multiplexer_4_out, or_3_out;
  wire [31:24] register_1_q;

  ROM #(.dataWidth(4)) rom_1 (.addr(instOut), .data(rom_1_data));
  Clock clock_1 (.out(clock_1_out));
  Counter #(.max('h7), .trigger("falling"), .width(3)) counter_1 (
    .Q(counter_1_q), .clk(and_1_out), .clr(or_1_out));  // open: load, D, count, carry, up
  and and_1 (and_1_out, delay_1_out_2, not_1_out);
  or or_1 (or_1_out, and_2_out, multiplexer_1_out[3]);
  delay delay_1 (.in_1(pull_resistor_1_node), .out_2(delay_1_out_2));
  and and_2 (and_2_out, multiplexer_1_out[1], in_5);
  Pull_Resistor pull_resistor_1 (.node(pull_resistor_1_node));
  Transistor transistor_1 (.in(clock_1_out), .out(pull_resistor_1_node), .gate(multiplexer_1_out[1]));
  ROM #(.addrWidth(3), .dataWidth(16)) rom_2 (.addr(counter_1_q), .data(rom_2_data));
  ROM #(.addrWidth(3), .dataWidth(16)) rom_3 (.addr(counter_1_q), .data(rom_3_data));
  ROM #(.addrWidth(3), .dataWidth(16)) rom_4 (.addr(counter_1_q), .data(rom_4_data));
  ROM #(.addrWidth(3), .dataWidth(16)) rom_5 (.addr(counter_1_q), .data(rom_5_data));
  Register inst (.D(in_1), .Q(instOut), .clk(delay_2_out_2), .clr(or_1_out));  // open: en
  Register instExtra (.D(in_1), .Q(instExtraOut), .clk(delay_3_out_2), .clr(or_1_out));  // open: en
  Register dReg (.D(in_1), .Q(dRegOut), .clk(delay_4_out_2), .clr(or_1_out));  // open: en
  Register sReg0 (.D(in_1), .Q(sReg0Out), .clk(delay_5_out_2), .clr(or_1_out));  // open: en
  Register sReg1 (.D(in_1), .Q(sReg1Out), .clk(delay_6_out_2), .clr(or_1_out));  // open: en
  Register data0 (.D(in_1), .Q(data[7:0]), .clk(delay_7_out_2), .clr(or_1_out));  // open: en
  Register data1 (.D(in_2), .Q(data[15:8]), .clk(delay_8_out_2), .clr(or_1_out));  // open: en
  Register data2 (.D(in_3), .Q(data[23:16]), .clk(delay_9_out_2), .clr(or_1_out));  // open: en
  Register data3 (.D(in_4), .Q(data[31:24]), .clk(delay_9_out_2), .clr(or_1_out));  // open: en
  delay delay_2 (.in_1(multiplexer_1_out[4]), .out_2(delay_2_out_2));
  delay delay_3 (.in_1(multiplexer_1_out[5]), .out_2(delay_3_out_2));
  delay delay_4 (.in_1(multiplexer_1_out[6]), .out_2(delay_4_out_2));
  delay delay_5 (.in_1(multiplexer_1_out[7]), .out_2(delay_5_out_2));
  delay delay_6 (.in_1(multiplexer_1_out[8]), .out_2(delay_6_out_2));
  delay delay_7 (.in_1(multiplexer_1_out[9]), .out_2(delay_7_out_2));
  delay delay_8 (.in_1(multiplexer_1_out[10]), .out_2(delay_8_out_2));
  delay delay_9 (.in_1(multiplexer_1_out[11]), .out_2(delay_9_out_2));
  ROM #(.addrWidth(3), .dataWidth(16)) rom_6 (.addr(counter_1_q), .data(rom_6_data));
  ROM #(.addrWidth(3), .dataWidth(16)) rom_7 (.addr(counter_1_q), .data(rom_7_data));
  ROM #(.addrWidth(3), .dataWidth(16)) rom_8 (.addr(counter_1_q), .data(rom_8_data));
  ROM #(.addrWidth(3), .dataWidth(16)) rom_9 (.addr(counter_1_q), .data(rom_9_data));
  delay delay_10 (.in_1(multiplexer_1_out[9]), .out_2(delay_10_out_2));
  delay delay_11 (.in_1(multiplexer_1_out[10]), .out_2(delay_11_out_2));
  delay delay_12 (.in_1(multiplexer_1_out[11]), .out_2(delay_12_out_2));
  not not_1 (not_1_out, multiplexer_1_out[0]);
  Multiplexer #(.enable("true"), .select(4), .width(16)) multiplexer_1 (
    .in0(rom_2_data), .in1(rom_3_data), .in2(rom_4_data), .in3(rom_5_data), .in4(rom_6_data),
    .in5(rom_7_data), .in6(rom_8_data), .in7(rom_9_data), .in8(rom_10_data), .in9(rom_11_data),
    .in10(rom_12_data), .in11(rom_13_data), .in12(rom_14_data), .in13(rom_15_data), .in14(rom_16_data),
    .in15(rom_17_data), .out(multiplexer_1_out), .sel(rom_1_data), .en(clock_1_out));
  delay delay_13 (.in_1(delay_10_out_2), .out_2(delay_13_out_2));
  delay delay_14 (.in_1(delay_13_out_2), .out_2(delay_14_out_2));
  delay delay_15 (.in_1(delay_11_out_2), .out_2(delay_15_out_2));
  delay delay_16 (.in_1(delay_15_out_2), .out_2(delay_16_out_2));
  delay delay_17 (.in_1(delay_12_out_2), .out_2(delay_17_out_2));
  delay delay_18 (.in_1(delay_17_out_2), .out_2(delay_18_out_2));
  or or_2 (or_2_out[0], multiplexer_1_out[4], multiplexer_1_out[5], multiplexer_1_out[6], multiplexer_1_out[7], multiplexer_1_out[8]);
  Pull_Resistor pull_resistor_2 (.node(pull_resistor_2_node));
  Priority_Encoder #(.select(2)) priority_encoder_1 (
    .in0(delay_14_out_2), .in1(delay_16_out_2), .in2(delay_18_out_2), .in3(delay_18_out_2),
    .out(priority_encoder_1_out));  // open: gs, en_out, en_in
  Pull_Resistor pull_resistor_3 (.node(priority_encoder_1_out));
  assign or_3_out = {pull_resistor_2_node, or_2_out[0]} | adder_1_out;  // OR_Gate or_3, 32 bits wide
  assign bit_extender_1_out = {{30{1'b0}}, priority_encoder_1_out};  // Bit_Extender bit_extender_1
  Adder #(.width(32)) adder_1 (.a(bit_extender_1_out), .b(32'h1), .out(adder_1_out));  // open: cin, cout
  ROM #(.addrWidth(3), .dataWidth(16)) rom_10 (.addr(counter_1_q), .data(rom_10_data));
  ROM #(.addrWidth(3), .dataWidth(16)) rom_11 (.addr(counter_1_q), .data(rom_11_data));
  ROM #(.addrWidth(3), .dataWidth(16)) rom_12 (.addr(counter_1_q), .data(rom_12_data));
  ROM #(.addrWidth(3), .dataWidth(16)) rom_13 (.addr(counter_1_q), .data(rom_13_data));
  Multiplexer #(.width(32)) multiplexer_2 (
    .in0(or_3_out), .in1(multiplexer_4_out), .out(multiplexer_2_out), .sel(delay_19_out_2));
  delay delay_19 (.in_1(delay_20_out_2), .out_2(delay_19_out_2));
  delay delay_20 (.in_1(multiplexer_1_out[13]), .out_2(delay_20_out_2));
  Pull_Resistor pull_resistor_4 (.node(pull_resistor_4_node));
  Adder #(.width(32)) adder_2 (.a(multiplexer_2_out), .b({register_1_q, out_6}), .out(adder_2_out));  // open: cin, cout
  Multiplexer #(.width(32)) multiplexer_3 (
    .in0(adder_2_out), .in1(multiplexer_4_out), .out(multiplexer_3_out), .sel(delay_21_out_2));
  delay delay_21 (.in_1(delay_22_out_2), .out_2(delay_21_out_2));
  delay delay_22 (.in_1(multiplexer_1_out[12]), .out_2(delay_22_out_2));
  Multiplexer #(.width(32)) multiplexer_4 (
    .in0(data), .out(multiplexer_4_out), .sel(pull_resistor_4_node));  // open: in1
  Register #(.trigger("falling"), .width(32)) register_1 (
    .D(multiplexer_3_out), .Q({register_1_q, out_6}), .clk(delay_23_out_2));  // open: en, clr
  delay delay_23 (.in_1(multiplexer_1_out[2]), .out_2(delay_23_out_2));
  ROM #(.addrWidth(3), .dataWidth(16)) rom_14 (.addr(counter_1_q), .data(rom_14_data));
  ROM #(.addrWidth(3), .dataWidth(16)) rom_15 (.addr(counter_1_q), .data(rom_15_data));
  ROM #(.addrWidth(3), .dataWidth(16)) rom_16 (.addr(counter_1_q), .data(rom_16_data));
  ROM #(.addrWidth(3), .dataWidth(16)) rom_17 (.addr(counter_1_q), .data(rom_17_data));
  T_Flip_Flop t_ff_1 (.Q(out_13), .preset(multiplexer_1_out[1]), .reset(or_1_out));  // open: clk, T, Qn

  // Notes on the sheet:
  //   contents of rom_1 (hex, n*v repeats v):
  //   0 1 2 3 4 5 6 7 8 9
  //   contents of rom_2 (hex, n*v repeats v):
  //   14 c
  //   contents of rom_3 (hex, n*v repeats v):
  //   14 44 e04 3
  //   contents of rom_4 (hex, n*v repeats v):
  //   14 44 604 3
  //   contents of rom_5 (hex, n*v repeats v):
  //   14 44 204 3
  //   contents of rom_6 (hex, n*v repeats v):
  //   14 1e04 c
  //   contents of rom_7 (hex, n*v repeats v):
  //   14 2e04 c
  //   contents of rom_8 (hex, n*v repeats v):
  //   14 24 44 84 e04 3
  //   contents of rom_9 (hex, n*v repeats v):
  //   14 24 44 84 604 3
  //   contents of rom_10 (hex, n*v repeats v):
  //   14 24 44 84 204 3
endmodule

module exec (
  input  [31:0] dataIn,
  input  [7:0] instIn,
  input  [7:0] instExtraIn,
  input  [7:0] dRegIn,
  input  [7:0] sReg0In,
  input  [7:0] sReg1In,
  input  in_7,
  input  opRdy,
  output out_9,
  output out_10,
  output [7:0] out_11,
  output memRead,
  output [1:0] memReadType,
  output [31:0] immOut,
  output [7:0] out_15,
  output [3:0] out_16,
  output [7:0] out_17,
  output [7:0] out_18,
  output [3:0] out_19,
  output [3:0] out_20,
  output enableComp,
  output initComp
);

  wire and_1_out, and_3_out, and_4_out, clock_1_out, delay_1_out_2, delay_2_out_2, delay_3_out_2,
       delay_4_out_2, delay_5_out_2, delay_6_out_2, delay_7_out_2, or_1_out, or_2_out, or_3_out,
       pull_resistor_1_node;
  wire [2:0] counter_1_q;
  wire [3:0] rom_1_data;
  wire [7:0] inst_q, or_4_out, undriven, undriven_2, undriven_3, xnor_1_out;
  wire [23:0] rom_2_data, rom_3_data, rom_4_data, rom_5_data, rom_6_data, rom_7_data, rom_8_data, rom_9_data,
       rom_10_data, rom_11_data, rom_12_data, rom_13_data, rom_14_data, rom_15_data, rom_16_data, rom_17_data;
  wire [23:12] multiplexer_1_out;

  and and_1 (and_1_out, out_9, in_7);
  or or_1 (or_1_out, and_1_out, delay_1_out_2);
  Register #(.width(32)) data (.D(dataIn), .Q(immOut), .clk(or_1_out));  // open: en, clr
  Register inst (.D(instIn), .Q(inst_q), .clk(or_1_out));  // open: en, clr
  Register instExtra (.D(instExtraIn), .Q(out_15), .clk(or_1_out));  // open: en, clr
  Register dReg (.D(dRegIn), .Q(out_11), .clk(or_1_out));  // open: en, clr
  Register sReg0 (.D(sReg0In), .Q(out_17), .clk(or_1_out));  // open: en, clr
  Register sReg1 (.D(sReg1In), .Q(out_18), .clk(or_1_out));  // open: en, clr
  and and_2 (memRead, clock_1_out, multiplexer_1_out[18]);
  delay delay_1 (.in_1(delay_2_out_2), .out_2(delay_1_out_2));
  Clock clock_1 (.out(clock_1_out));
  delay delay_2 (.in_1(delay_3_out_2), .out_2(delay_2_out_2));
  delay delay_3 (.in_1(delay_4_out_2), .out_2(delay_3_out_2));
  delay delay_4 (.in_1(multiplexer_1_out[20]), .out_2(delay_4_out_2));
  and and_3 (and_3_out, pull_resistor_1_node, or_3_out);
  Pull_Resistor pull_resistor_1 (.node(pull_resistor_1_node));
  Transistor transistor_1 (.in(clock_1_out), .out(pull_resistor_1_node), .gate(multiplexer_1_out[13]));
  Counter #(.max('h7), .trigger("falling"), .width(3)) counter_1 (
    .Q(counter_1_q), .clk(and_3_out), .clr(or_2_out));  // open: load, D, count, carry, up
  or or_2 (or_2_out, and_4_out, multiplexer_1_out[12]);
  and and_4 (and_4_out, multiplexer_1_out[13], in_7);
  or or_3 (or_3_out, opRdy, ~enableComp);  // OR_Gate
  T_Flip_Flop t_ff_1 (.Qn(out_9), .preset(multiplexer_1_out[13]), .reset(or_2_out));  // open: clk, T, Q
  T_Flip_Flop t_ff_2 (.preset(enableComp));  // open: clk, T, Q, Qn, reset
  ROM #(.dataWidth(4)) rom_1 (.addr(inst_q), .data(rom_1_data));
  delay delay_5 (.in_1(clock_1_out), .out_2(delay_5_out_2));
  delay delay_6 (.in_1(delay_5_out_2), .out_2(delay_6_out_2));
  delay delay_7 (.in_1(delay_6_out_2), .out_2(delay_7_out_2));
  ROM #(.addrWidth(3), .dataWidth(24)) rom_2 (.addr(counter_1_q), .data(rom_2_data));
  ROM #(.addrWidth(3), .dataWidth(24)) rom_3 (.addr(counter_1_q), .data(rom_3_data));
  ROM #(.addrWidth(3), .dataWidth(24)) rom_4 (.addr(counter_1_q), .data(rom_4_data));
  ROM #(.addrWidth(3), .dataWidth(24)) rom_5 (.addr(counter_1_q), .data(rom_5_data));
  ROM #(.addrWidth(3), .dataWidth(24)) rom_6 (.addr(counter_1_q), .data(rom_6_data));
  ROM #(.addrWidth(3), .dataWidth(24)) rom_7 (.addr(counter_1_q), .data(rom_7_data));
  ROM #(.addrWidth(3), .dataWidth(24)) rom_8 (.addr(counter_1_q), .data(rom_8_data));
  ROM #(.addrWidth(3), .dataWidth(24)) rom_9 (.addr(counter_1_q), .data(rom_9_data));
  Multiplexer #(.enable("true"), .select(4), .width(24)) multiplexer_1 (
    .in0(rom_2_data), .in1(rom_3_data), .in2(rom_4_data), .in3(rom_5_data), .in4(rom_6_data),
    .in5(rom_7_data), .in6(rom_8_data), .in7(rom_9_data), .in8(rom_10_data), .in9(rom_11_data),
    .in10(rom_12_data), .in11(rom_13_data), .in12(rom_14_data), .in13(rom_15_data), .in14(rom_16_data),
    .in15(rom_17_data),
    .out({multiplexer_1_out[23:20], out_10, multiplexer_1_out[18], memReadType, initComp, enableComp, multiplexer_1_out[13:12], out_19, out_20, out_16}),
    .sel(rom_1_data), .en(delay_7_out_2));
  assign or_4_out = ~undriven | xnor_1_out;  // OR_Gate or_4, 8 bits wide
  assign xnor_1_out = ~(undriven_2 ^ undriven_3);  // XNOR_Gate xnor_1, 8 bits wide
  ROM #(.addrWidth(3), .dataWidth(24)) rom_10 (.addr(counter_1_q), .data(rom_10_data));
  ROM #(.addrWidth(3), .dataWidth(24)) rom_11 (.addr(counter_1_q), .data(rom_11_data));
  ROM #(.addrWidth(3), .dataWidth(24)) rom_12 (.addr(counter_1_q), .data(rom_12_data));
  ROM #(.addrWidth(3), .dataWidth(24)) rom_13 (.addr(counter_1_q), .data(rom_13_data));
  ROM #(.addrWidth(3), .dataWidth(24)) rom_14 (.addr(counter_1_q), .data(rom_14_data));
  ROM #(.addrWidth(3), .dataWidth(24)) rom_15 (.addr(counter_1_q), .data(rom_15_data));
  ROM #(.addrWidth(3), .dataWidth(24)) rom_16 (.addr(counter_1_q), .data(rom_16_data));
  ROM #(.addrWidth(3), .dataWidth(24)) rom_17 (.addr(counter_1_q), .data(rom_17_data));

  // Notes on the sheet:
  //   contents of rom_1 (hex, n*v repeats v):
  //   0 1 4*0 2
  //   contents of rom_2 (hex, n*v repeats v):
  //   1000
  //   contents of rom_3 (hex, n*v repeats v):
  //   181000
  //   contents of rom_4 (hex, n*v repeats v):
  //   8001 4011
endmodule

module memRead (
  input  [31:0] address,
  input  [1:0] in_2,
  input  in_3,
  input  [7:0] in_4,
  input  [7:0] in_5,
  input  [7:0] in_6,
  input  [7:0] in_7,
  output [31:0] data,
  output [23:0] out_9
);

  wire decoder_1_out1, decoder_1_out2, decoder_1_out3, delay_1_out_2, delay_2_out_2, delay_3_out_2,
       delay_4_out_2, or_1_out, or_2_out;
  wire [7:0] controlled_buffer_1_out, controlled_buffer_2_out, controlled_buffer_3_out,
       controlled_buffer_4_out;

  assign controlled_buffer_1_out = or_1_out ? in_4 : 8'bz;  // Controlled_Buffer controlled_buffer_1
  assign controlled_buffer_2_out = or_2_out ? in_5 : 8'bz;  // Controlled_Buffer controlled_buffer_2
  assign controlled_buffer_3_out = decoder_1_out3 ? in_6 : 8'bz;  // Controlled_Buffer controlled_buffer_3
  assign controlled_buffer_4_out = decoder_1_out3 ? in_7 : 8'bz;  // Controlled_Buffer controlled_buffer_4
  Pull_Resistor pull_resistor_1 (.node(controlled_buffer_1_out));
  Pull_Resistor pull_resistor_2 (.node(controlled_buffer_2_out));
  Pull_Resistor pull_resistor_3 (.node(controlled_buffer_3_out));
  Pull_Resistor pull_resistor_4 (.node(controlled_buffer_4_out));
  or or_1 (or_1_out, decoder_1_out1, or_2_out);
  or or_2 (or_2_out, decoder_1_out2, decoder_1_out3);
  Decoder #(.select(2)) decoder_1 (
    .out1(decoder_1_out1), .out2(decoder_1_out2), .out3(decoder_1_out3), .sel(in_2));  // open: out0, en
  Register #(.trigger("falling"), .width(32)) register_1 (
    .D({controlled_buffer_4_out, controlled_buffer_3_out, controlled_buffer_2_out, controlled_buffer_1_out}),
    .Q(data), .clk(delay_4_out_2));  // open: en, clr
  delay delay_1 (.in_1(in_3), .out_2(delay_1_out_2));
  delay delay_2 (.in_1(delay_1_out_2), .out_2(delay_2_out_2));
  delay delay_3 (.in_1(delay_2_out_2), .out_2(delay_3_out_2));
  delay delay_4 (.in_1(delay_3_out_2), .out_2(delay_4_out_2));

  assign out_9 = address[23:0];
endmodule
