// Logisim project CUPU.circ as structural Verilog: 15 circuits, main circuit main
module main (
);

  wire cpu_1_out_4;
  wire [7:0] cpu_1_out_2, ram_1_dout;
  wire [23:0] bit_extender_1_out;
  wire [31:0] cpu_1_out_3;

  RAM #(.addrWidth(24), .enables("line"), .\type ("nonvolatile")) ram_1 (
    .addr(bit_extender_1_out), .we(cpu_1_out_4), .clk(cpu_1_out_4), .din(cpu_1_out_2), .dout(ram_1_dout));
  Bit_Extender #(.in_width(32), .out_width(24)) bit_extender_1 (.in(cpu_1_out_3), .out(bit_extender_1_out));
  cpu cpu_1 (.in_1(ram_1_dout), .out_2(cpu_1_out_2), .out_3(cpu_1_out_3), .out_4(cpu_1_out_4));
endmodule

module control (
  input  [7:0] in_1,
  input  [7:0] flag_mask,
  input  [7:0] flag,
  input  [7:0] flag_ref,
  input  clk,
  input  rsm,
  output set_sp,
  output mod1,
  output mod0,
  output use_imm,
  output flags_sel,
  output [1:0] sel_a,
  output write_pc,
  output inc_pc,
  output [1:0] sel_d_out,
  output [3:0] sel_bus_d_s,
  output [3:0] sel_inb_reg,
  output fpu_init,
  output alu_init,
  output stack_offs,
  output set_ra,
  output out_22,
  output set_fp,
  output set_a_max,
  output set_a_reg,
  output set_d_out,
  output del_d_in,
  output inb_save,
  output fpu_enable,
  output alu_enable,
  output store,
  output load
);

  wire and_1_out, and_3_out, and_4_out, controlled_buffer_1_out, delay_1_out_2, not_1_out, or_2_out,
       or_3_out, or_4_out, or_5_out, or_6_out, or_7_out, or_8_out, or_9_out, t_ff_1_qn, xnor_1_out,
       xnor_2_out, xnor_3_out, xnor_4_out, xnor_5_out, xnor_6_out, xnor_7_out, xnor_8_out;
  wire [3:0] multiplexer_1_out;
  wire [5:0] counter_1_q;
  wire [22:14] multiplexer_1_out_2;
  wire [25:0] rom_1_data, rom_2_data, rom_3_data, rom_4_data, rom_5_data, rom_6_data, rom_7_data, rom_8_data,
       rom_9_data, rom_10_data, rom_11_data, rom_12_data, rom_13_data, rom_14_data, rom_15_data, rom_16_data,
       rom_17_data, rom_18_data, rom_19_data, rom_20_data, rom_21_data, rom_22_data, rom_23_data,
       rom_24_data, rom_25_data, rom_26_data, rom_27_data, rom_28_data, rom_29_data, rom_30_data,
       rom_31_data, rom_32_data;

  assign controlled_buffer_1_out = t_ff_1_qn ? clk : 1'bz;  // Controlled_Buffer controlled_buffer_1
  T_Flip_Flop t_ff_1 (.Qn(t_ff_1_qn), .preset(multiplexer_1_out_2[22]), .reset(rsm));  // open: clk, T, Q
  not not_1 (not_1_out, controlled_buffer_1_out);
  and and_1 (and_1_out, not_1_out, multiplexer_1_out_2[20]);
  ROM #(.addrWidth(6), .dataWidth(26)) rom_1 (.addr(counter_1_q), .data(rom_1_data));
  Counter #(.max('h3f), .width(6)) counter_1 (
    .Q(counter_1_q), .clk(controlled_buffer_1_out), .clr(and_1_out));  // open: load, D, count, carry, up
  ROM #(.addrWidth(6), .dataWidth(26)) rom_2 (.addr(counter_1_q), .data(rom_2_data));
  Pull_Resistor pull_resistor_1 (.node(controlled_buffer_1_out));
  ROM #(.addrWidth(6), .dataWidth(26)) rom_3 (.addr(counter_1_q), .data(rom_3_data));
  ROM #(.addrWidth(6), .dataWidth(26)) rom_4 (.addr(counter_1_q), .data(rom_4_data));
  ROM #(.addrWidth(6), .dataWidth(26)) rom_5 (.addr(counter_1_q), .data(rom_5_data));
  ROM #(.addrWidth(6), .dataWidth(26)) rom_6 (.addr(counter_1_q), .data(rom_6_data));
  ROM #(.addrWidth(6), .dataWidth(26)) rom_7 (.addr(counter_1_q), .data(rom_7_data));
  ROM #(.addrWidth(6), .dataWidth(26)) rom_8 (.addr(counter_1_q), .data(rom_8_data));
  or or_1 (write_pc, multiplexer_1_out_2[15], and_3_out);
  and and_2 (inc_pc, delay_1_out_2, multiplexer_1_out_2[14]);
  delay delay_1 (.in_1(controlled_buffer_1_out), .out_2(delay_1_out_2));
  ROM #(.addrWidth(6), .dataWidth(26)) rom_9 (.addr(counter_1_q), .data(rom_9_data));
  ROM #(.addrWidth(6), .dataWidth(26)) rom_10 (.addr(counter_1_q), .data(rom_10_data));
  ROM #(.addrWidth(6), .dataWidth(26)) rom_11 (.addr(counter_1_q), .data(rom_11_data));
  ROM #(.addrWidth(6), .dataWidth(26)) rom_12 (.addr(counter_1_q), .data(rom_12_data));
  ROM #(.addrWidth(6), .dataWidth(26)) rom_13 (.addr(counter_1_q), .data(rom_13_data));
  ROM #(.addrWidth(6), .dataWidth(26)) rom_14 (.addr(counter_1_q), .data(rom_14_data));
  ROM #(.addrWidth(6), .dataWidth(26)) rom_15 (.addr(counter_1_q), .data(rom_15_data));
  ROM #(.addrWidth(6), .dataWidth(26)) rom_16 (.addr(counter_1_q), .data(rom_16_data));
  Multiplexer #(.select(5), .width(26)) multiplexer_1 (
    .in0(rom_1_data), .in1(rom_2_data), .in2(rom_3_data), .in3(rom_4_data), .in4(rom_5_data),
    .in5(rom_6_data), .in6(rom_7_data), .in7(rom_8_data), .in8(rom_9_data), .in9(rom_10_data),
    .in10(rom_11_data), .in11(rom_12_data), .in12(rom_13_data), .in13(rom_14_data), .in14(rom_15_data),
    .in15(rom_16_data), .in16(rom_17_data), .in17(rom_18_data), .in18(rom_19_data), .in19(rom_20_data),
    .in20(rom_21_data), .in21(rom_22_data), .in22(rom_23_data), .in23(rom_24_data), .in24(rom_25_data),
    .in25(rom_26_data), .in26(rom_27_data), .in27(rom_28_data), .in28(rom_29_data), .in29(rom_30_data),
    .in30(rom_31_data), .in31(rom_32_data),
    .out({set_sp, mod1, mod0, multiplexer_1_out_2[22:20], use_imm, flags_sel, sel_a, multiplexer_1_out_2[15:14], sel_d_out, sel_bus_d_s, sel_inb_reg, multiplexer_1_out}),
    .sel(in_1[4:0]));
  or or_2 (or_2_out, ~flag_mask[0], xnor_1_out);  // OR_Gate
  or or_3 (or_3_out, ~flag_mask[1], xnor_3_out);  // OR_Gate
  xnor xnor_1 (xnor_1_out, flag[0], flag_ref[0]);
  and and_3 (and_3_out, multiplexer_1_out_2[21], and_4_out);
  or or_4 (or_4_out, ~flag_mask[2], xnor_2_out);  // OR_Gate
  xnor xnor_2 (xnor_2_out, flag[2], flag_ref[2]);
  xnor xnor_3 (xnor_3_out, flag[1], flag_ref[1]);
  Decoder #(.select(4)) decoder_1 (
    .out1(load), .out2(store), .out3(alu_enable), .out4(fpu_enable), .out5(inb_save), .out6(del_d_in),
    .out7(set_d_out), .out8(set_a_reg), .out9(set_a_max), .out10(set_fp), .out11(out_22), .out12(set_ra),
    .out13(stack_offs), .out14(alu_init), .out15(fpu_init), .sel(multiplexer_1_out));  // open: out0, en
  and and_4 (and_4_out, or_2_out, or_3_out, or_4_out, or_5_out, or_6_out, or_7_out, or_8_out, or_9_out);
  or or_5 (or_5_out, ~flag_mask[3], xnor_4_out);  // OR_Gate
  or or_6 (or_6_out, ~flag_mask[4], xnor_5_out);  // OR_Gate
  xnor xnor_4 (xnor_4_out, flag[3], flag_ref[3]);
  xnor xnor_5 (xnor_5_out, flag[4], flag_ref[4]);
  or or_7 (or_7_out, ~flag_mask[5], xnor_6_out);  // OR_Gate
  xnor xnor_6 (xnor_6_out, flag[5], flag_ref[5]);
  ROM #(.addrWidth(6), .dataWidth(26)) rom_17 (.addr(counter_1_q), .data(rom_17_data));
  ROM #(.addrWidth(6), .dataWidth(26)) rom_18 (.addr(counter_1_q), .data(rom_18_data));
  ROM #(.addrWidth(6), .dataWidth(26)) rom_19 (.addr(counter_1_q), .data(rom_19_data));
  ROM #(.addrWidth(6), .dataWidth(26)) rom_20 (.addr(counter_1_q), .data(rom_20_data));
  ROM #(.addrWidth(6), .dataWidth(26)) rom_21 (.addr(counter_1_q), .data(rom_21_data));
  ROM #(.addrWidth(6), .dataWidth(26)) rom_22 (.addr(counter_1_q), .data(rom_22_data));
  ROM #(.addrWidth(6), .dataWidth(26)) rom_23 (.addr(counter_1_q), .data(rom_23_data));
  ROM #(.addrWidth(6), .dataWidth(26)) rom_24 (.addr(counter_1_q), .data(rom_24_data));
  or or_8 (or_8_out, ~flag_mask[6], xnor_7_out);  // OR_Gate
  or or_9 (or_9_out, ~flag_mask[7], xnor_8_out);  // OR_Gate
  xnor xnor_7 (xnor_7_out, flag[6], flag_ref[6]);
  xnor xnor_8 (xnor_8_out, flag_ref[7], flag[7]);
  ROM #(.addrWidth(6), .dataWidth(26)) rom_25 (.addr(counter_1_q), .data(rom_25_data));
  ROM #(.addrWidth(6), .dataWidth(26)) rom_26 (.addr(counter_1_q), .data(rom_26_data));
  ROM #(.addrWidth(6), .dataWidth(26)) rom_27 (.addr(counter_1_q), .data(rom_27_data));
  ROM #(.addrWidth(6), .dataWidth(26)) rom_28 (.addr(counter_1_q), .data(rom_28_data));
  ROM #(.addrWidth(6), .dataWidth(26)) rom_29 (.addr(counter_1_q), .data(rom_29_data));
  ROM #(.addrWidth(6), .dataWidth(26)) rom_30 (.addr(counter_1_q), .data(rom_30_data));
  ROM #(.addrWidth(6), .dataWidth(26)) rom_31 (.addr(counter_1_q), .data(rom_31_data));
  ROM #(.addrWidth(6), .dataWidth(26)) rom_32 (.addr(counter_1_q), .data(rom_32_data));

  // Notes on the sheet:
  //   jmpregal
  //   inttfltfltcmpcjmp
  //   flttrnctintintcmpcjmp
  //   fltrndtintintcmpcjmp
  //   contents of rom_1 (hex, n*v repeats v):
  //   104075
  //   contents of rom_2 (hex, n*v repeats v):
  //   75 4000 40b5 40c5 40d5 40e5 40f5 100001
  //   contents of rom_3 (hex, n*v repeats v):
  //   75 4000 4085 40b5 40a5 40c5 40d5 40e5 40f5 8000e 480003 100201
  //   contents of rom_4 (hex, n*v repeats v):
  //   75 4000 4085 40b5 40c5 40d5 40e5 f5 300000
  //   contents of rom_5 (hex, n*v repeats v):
  //   75 4000 4085 40b5 4095 40a5 e 400003 100201
  //   contents of rom_6 (hex, n*v repeats v):
  //   75 4000 4085 40b5 40a5 40c5 40d5 40e5 40f5 8000f 480004 100801
  //   contents of rom_7 (hex, n*v repeats v):
  //   75 4000 4085 40b5 40c5 40d5 40e5 f5 340000
  //   contents of rom_8 (hex, n*v repeats v):
  //   75 4000 4085 40b5 4095 40a5 f 400004 100801
  //   contents of rom_9 (hex, n*v repeats v):
  //   75 4000 40b5 4095 100101
  //   contents of rom_10 (hex, n*v repeats v):
  //   75 4000 4095 40c5 40d5 40e5 40f5 8 107 10002 11002 12002 13002 100000
  //   contents of rom_11 (hex, n*v repeats v):
  //   75 4000 40c5 40d5 40e5 f5 108000
  //   contents of rom_12 (hex, n*v repeats v):
  //   75 4000 40c5 40d5 40e5 40f5 60c 108000
  //   contents of rom_13 (hex, n*v repeats v):
  //   75 108700
  //   contents of rom_14 (hex, n*v repeats v):
  //   75 4000 40b5 100701
  //   contents of rom_15 (hex, n*v repeats v):
  //   75 4000 0 40c5 40d5 40e5 40f5 7 3000002 1801002 1802002 1803002 100000
endmodule

module fpu (
  input  enable,
  input  [4:0] op,
  input  [31:0] a,
  input  [31:0] b,
  input  init,
  input  clk,
  output [31:0] result,
  output [7:0] flags,
  output rsm
);

  wire and_1_out, cordic_trig_1_resume, delay_1_out_2, fpnegator_1_p2, fpnegator_1_p3, fpnegator_1_p4,
       fpnegator_1_p5, inv_sqrt_1_inpt_zero, inv_sqrt_1_nan, ln_1_resume, nrt_1_out_6, potenz_float_1_resume,
       pull_resistor_1_node, sqrt_1_resume, undriven, undriven_2;
  wire [4:0] bit_extender_1_out, bit_extender_2_out;
  wire [7:0] multiplexer_3_out_2;
  wire [30:1] multiplexer_3_out;
  wire [31:0] cordic_trig_1_cos, cordic_trig_1_sin, cordic_trig_1_tan, fpadder_1_out, fpadder_2_out,
       fpdivider_1_out, fpmultiplier_1_out, fpnegator_1_p6, fpsubtractor_1_out, fpsubtractor_2_out,
       inttofp_1_p2, inttofp_1_p3, inv_sqrt_1_aprox, ln_1_out_4, nrt_1_out_5, potenz_float_1_res,
       shifter_1_out, shifter_2_out, sqrt_1_res;

  Bit_Extender #(.in_width(32), .out_width(5)) bit_extender_1 (.in(b), .out(bit_extender_1_out));
  Bit_Extender #(.in_width(32), .out_width(5)) bit_extender_2 (.in(b), .out(bit_extender_2_out));
  // Random #(.width(32)) random_1: pin names not known; wires that end beside it: 1'b1, enable
  Pull_Resistor pull_resistor_1 (.node(pull_resistor_1_node));
  assign pull_resistor_1_node = enable ? clk : 1'bz;  // Controlled_Buffer controlled_buffer_1
  FPAdder fpadder_1 (.a(a), .b(b), .out(fpadder_1_out));
  FPSubtractor fpsubtractor_1 (.a(a), .b(b), .out(fpsubtractor_1_out));
  FPMultiplier fpmultiplier_1 (.a(a), .b(b), .out(fpmultiplier_1_out));
  FPDivider fpdivider_1 (.a(a), .b(b), .out(fpdivider_1_out));
  FPAdder fpadder_2 (.a(a), .b(32'h1), .out(fpadder_2_out));
  FPSubtractor fpsubtractor_2 (.a(a), .b(32'h1), .out(fpsubtractor_2_out));
  // FPNegator fpnegator_1: pin names not known; wires that end beside it: a, fpnegator_1_p2, fpnegator_1_p3, fpnegator_1_p4, fpnegator_1_p5, fpnegator_1_p6
  Shifter #(.width(32)) shifter_1 (.in(a), .\dist (bit_extender_1_out), .out(shifter_1_out));
  Shifter #(.shift("lr"), .width(32)) shifter_2 (.in(a), .\dist (bit_extender_2_out), .out(shifter_2_out));
  // IntToFP #(.width(32)) inttofp_1: pin names not known; wires that end beside it: a, inttofp_1_p2, inttofp_1_p3
  inv_sqrt inv_sqrt_1 (.in_1(a), .aprox(inv_sqrt_1_aprox), .NaN(inv_sqrt_1_nan), .inpt_zero(inv_sqrt_1_inpt_zero));
  cordic_trig cordic_trig_1 (
    .ang(a), .reset(init), .takt(pull_resistor_1_node), .cos(cordic_trig_1_cos), .sin(cordic_trig_1_sin),
    .tan(cordic_trig_1_tan), .resume(cordic_trig_1_resume));
  sqrt sqrt_1 (.root(a), .reset(init), .takt(pull_resistor_1_node), .res(sqrt_1_res), .resume(sqrt_1_resume));
  potenz_float potenz_float_1 (
    .inpt(a), .power(b), .reset(init), .takt(pull_resistor_1_node), .res(potenz_float_1_res),
    .resume(potenz_float_1_resume));
  nrt nrt_1 (.x(a), .deg(b), .in_3(init), .in_4(pull_resistor_1_node), .out_5(nrt_1_out_5), .out_6(nrt_1_out_6));
  ln ln_1 (.x(a), .reset(init), .clk(pull_resistor_1_node), .out_4(ln_1_out_4), .resume(ln_1_resume));
  Pull_Resistor pull_resistor_2 (.node(multiplexer_3_out_2[3]));
  Multiplexer #(.select(5)) multiplexer_1 (
    .in0(undriven), .in1(undriven_2), .in2(fpnegator_1_p2), .in3(fpnegator_1_p3), .in4(fpnegator_1_p4),
    .in5(fpnegator_1_p5), .in6(inv_sqrt_1_nan), .in7(inv_sqrt_1_inpt_zero), .out(multiplexer_3_out_2[3]),
    .sel(op));  // open: in8, in9, in10, in11, in12, in13, in14, in15, in16, in17, in18, in19, in20, in21, in22, in23, in24, in25, in26, in27, in28, in29, in30, in31
  Multiplexer #(.select(5)) multiplexer_2 (
    .in0(1'b1), .in1(1'b1), .in2(1'b1), .in3(1'b1), .in4(1'b1), .in5(1'b1), .in6(1'b1), .in7(1'b1),
    .in8(1'b1), .in9(1'b1), .in10(1'b1), .in11(1'b1), .in12(cordic_trig_1_resume),
    .in13(cordic_trig_1_resume), .in14(cordic_trig_1_resume), .in15(sqrt_1_resume),
    .in16(potenz_float_1_resume), .in17(nrt_1_out_6), .in18(ln_1_resume), .in19(1'b1), .in20(1'b1),
    .in21(1'b1), .in22(1'b1), .in23(1'b1), .in24(1'b1), .in25(1'b1), .in26(1'b1), .in27(1'b1), .in28(1'b1),
    .in29(1'b1), .in30(1'b1), .in31(1'b1), .out(rsm), .sel(op));
  Multiplexer #(.select(5), .width(32)) multiplexer_3 (
    .in0(fpadder_1_out), .in1(fpsubtractor_1_out), .in2(fpmultiplier_1_out), .in3(fpdivider_1_out),
    .in4(fpadder_2_out), .in5(fpsubtractor_2_out), .in6(fpnegator_1_p6), .in7(shifter_1_out),
    .in8(shifter_2_out), .in9(inttofp_1_p2), .in10(inttofp_1_p3), .in11(inv_sqrt_1_aprox),
    .in12(cordic_trig_1_cos), .in13(cordic_trig_1_sin), .in14(cordic_trig_1_tan), .in15(sqrt_1_res),
    .in16(potenz_float_1_res), .in17(nrt_1_out_5), .in18(ln_1_out_4),
    .out({multiplexer_3_out_2[1], multiplexer_3_out, multiplexer_3_out_2[0]}), .sel(op));  // open: in19, in20, in21, in22, in23, in24, in25, in26, in27, in28, in29, in30, in31
  // FPComparator fpcomparator_1: pin names not known; wires that end beside it: {multiplexer_3_out_2[1], multiplexer_3_out, multiplexer_3_out_2[0]}, {32{1'b0}}, multiplexer_3_out_2[2]
  // FPComparator fpcomparator_2: pin names not known; wires that end beside it: {multiplexer_3_out_2[1], multiplexer_3_out, multiplexer_3_out_2[0]}, {32{1'b1}}, multiplexer_3_out_2[4]
  // FPComparator fpcomparator_3: pin names not known; wires that end beside it: a, b, multiplexer_3_out_2[5], multiplexer_3_out_2[6], multiplexer_3_out_2[7]
  and and_1 (and_1_out, enable, rsm);
  Register register_1 (.D(multiplexer_3_out_2), .Q(flags), .clk(delay_1_out_2));  // open: en, clr
  delay delay_1 (.in_1(and_1_out), .out_2(delay_1_out_2));
  // Probe on result
  Register #(.width(32)) register_2 (
    .D({multiplexer_3_out_2[1], multiplexer_3_out, multiplexer_3_out_2[0]}), .Q(result), .clk(delay_1_out_2));  // open: en, clr
endmodule

module alu (
  input  enable,
  input  [4:0] op,
  input  [31:0] a,
  input  [31:0] b,
  input  init,
  input  clk,
  output [31:0] result,
  output [7:0] flags,
  output rsm
);

  wire adder_1_cout, adder_2_cout, and_2_out, delay_1_out_2, multiplexer_3_out, potenz_int_1_resume,
       pull_resistor_1_node, subtractor_1_bout, subtractor_2_bout;
  wire [4:0] bit_extender_1_out, bit_extender_2_out;
  wire [7:0] multiplexer_1_out_2;
  wire [30:1] multiplexer_1_out;
  wire [31:0] adder_1_out, adder_2_out, and_1_out, divider_1_out, divider_1_rem, fptoint_1_p3, fptoint_1_p4,
       multiplier_1_cout, multiplier_1_out, nand_1_out, negator_1_out, nor_1_out, not_1_out, or_1_out,
       potenz_int_1_res, shifter_1_out, shifter_2_out, subtractor_1_out, subtractor_2_out, xnor_1_out,
       xor_1_out;

  Bit_Extender #(.in_width(32), .out_width(5)) bit_extender_1 (.in(b), .out(bit_extender_1_out));
  Bit_Extender #(.in_width(32), .out_width(5)) bit_extender_2 (.in(b), .out(bit_extender_2_out));
  Random #(.width(32)) random_1 ();  // open: clk, next, out, clr
  Pull_Resistor pull_resistor_1 (.node(pull_resistor_1_node));
  assign pull_resistor_1_node = enable ? clk : 1'bz;  // Controlled_Buffer controlled_buffer_1
  Adder #(.width(32)) adder_1 (.a(a), .b(b), .out(adder_1_out), .cout(adder_1_cout));  // open: cin
  Subtractor #(.width(32)) subtractor_1 (.a(a), .b(b), .out(subtractor_1_out), .bout(subtractor_1_bout));  // open: bin
  Multiplier #(.width(32)) multiplier_1 (.a(a), .b(b), .out(multiplier_1_out), .cout(multiplier_1_cout));  // open: cin
  Divider #(.width(32)) divider_1 (.a(a), .b(b), .out(divider_1_out), .rem(divider_1_rem));  // open: upper
  Adder #(.width(32)) adder_2 (.a(a), .b(32'h1), .out(adder_2_out), .cout(adder_2_cout));  // open: cin
  Subtractor #(.width(32)) subtractor_2 (
    .a(a), .b(32'h1), .out(subtractor_2_out), .bout(subtractor_2_bout));  // open: bin
  Negator #(.width(32)) negator_1 (.in(a), .out(negator_1_out));
  Shifter #(.width(32)) shifter_1 (.in(a), .\dist (bit_extender_1_out), .out(shifter_1_out));
  Shifter #(.shift("lr"), .width(32)) shifter_2 (.in(a), .\dist (bit_extender_2_out), .out(shifter_2_out));
  assign or_1_out = a | b;  // OR_Gate or_1, 32 bits wide
  assign and_1_out = a & b;  // AND_Gate and_1, 32 bits wide
  assign xor_1_out = a ^ b;  // XOR_Gate xor_1, 32 bits wide
  assign not_1_out = ~a;  // NOT_Gate not_1, 32 bits wide
  assign nor_1_out = ~(a | b);  // NOR_Gate nor_1, 32 bits wide
  assign nand_1_out = ~(a & b);  // NAND_Gate nand_1, 32 bits wide
  assign xnor_1_out = ~(a ^ b);  // XNOR_Gate xnor_1, 32 bits wide
  // FPToInt #(.width(32)) fptoint_1: pin names not known; wires that end beside it: a, enable, fptoint_1_p3, fptoint_1_p4
  potenz_int potenz_int_1 (
    .inpt(a), .power(b), .reset(init), .takt(pull_resistor_1_node), .res(potenz_int_1_res),
    .resume(potenz_int_1_resume));
  Multiplexer #(.select(5), .width(32)) multiplexer_1 (
    .in0(adder_1_out), .in1(subtractor_1_out), .in2(multiplier_1_out), .in3(divider_1_out),
    .in4(adder_2_out), .in5(subtractor_2_out), .in6(negator_1_out), .in7(shifter_1_out), .in8(shifter_2_out),
    .in9(or_1_out), .in10(and_1_out), .in11(xor_1_out), .in12(not_1_out), .in13(nor_1_out),
    .in14(nand_1_out), .in15(xnor_1_out), .in16(fptoint_1_p3), .in17(fptoint_1_p4), .in18(a),
    .in19(multiplier_1_cout), .in20(divider_1_rem), .in21(potenz_int_1_res),
    .out({multiplexer_1_out_2[1], multiplexer_1_out, multiplexer_1_out_2[0]}), .sel(op));  // open: in22, in23, in24, in25, in26, in27, in28, in29, in30, in31
  Multiplexer #(.select(5)) multiplexer_2 (
    .in0(adder_1_cout), .in1(subtractor_1_bout), .in4(adder_2_cout), .in5(subtractor_2_bout),
    .out(multiplexer_1_out_2[3]), .sel(op));  // open: in2, in3, in6, in7, in8, in9, in10, in11, in12, in13, in14, in15, in16, in17, in18, in19, in20, in21, in22, in23, in24, in25, in26, in27, in28, in29, in30, in31
  Multiplexer #(.select(5)) multiplexer_3 (
    .in0(1'b1), .in1(1'b1), .in2(1'b1), .in3(1'b1), .in4(1'b1), .in5(1'b1), .in6(1'b1), .in7(1'b1),
    .in8(1'b1), .in9(1'b1), .in10(1'b1), .in11(1'b1), .in12(1'b1), .in13(1'b1), .in14(1'b1), .in15(1'b1),
    .in16(1'b1), .in17(1'b1), .in18(1'b1), .in19(1'b1), .in20(1'b1), .in21(potenz_int_1_resume), .in22(1'b1),
    .in23(1'b1), .in24(1'b1), .in25(1'b1), .in26(1'b1), .in27(1'b1), .in28(1'b1), .in29(1'b1), .in30(1'b1),
    .in31(1'b1), .out(multiplexer_3_out), .sel(op));
  and and_2 (and_2_out, enable, multiplexer_3_out);
  Comparator #(.width(32)) comparator_1 (
    .a({multiplexer_1_out_2[1], multiplexer_1_out, multiplexer_1_out_2[0]}), .b({32{1'b0}}),
    .eq(multiplexer_1_out_2[2]));  // open: gt, lt
  Comparator #(.width(32)) comparator_2 (
    .a({multiplexer_1_out_2[1], multiplexer_1_out, multiplexer_1_out_2[0]}), .b({32{1'b1}}),
    .eq(multiplexer_1_out_2[4]));  // open: gt, lt
  Comparator #(.width(32)) comparator_3 (
    .a(a), .b(b), .gt(multiplexer_1_out_2[5]), .eq(multiplexer_1_out_2[6]), .lt(multiplexer_1_out_2[7]));
  Pull_Resistor pull_resistor_2 (.node(multiplexer_1_out_2));
  delay delay_1 (.in_1(multiplexer_3_out), .out_2(delay_1_out_2));
  Register #(.width(32)) register_1 (
    .D({multiplexer_1_out_2[1], multiplexer_1_out, multiplexer_1_out_2[0]}), .Q(result), .clk(and_2_out));  // open: en, clr
  Register register_2 (.D(multiplexer_1_out_2), .Q(flags), .clk(and_2_out));  // open: en, clr
  delay delay_2 (.in_1(delay_1_out_2), .out_2(rsm));
endmodule

module regs (
  input  [7:0] s0_sel,
  input  [7:0] s1_sel,
  input  [7:0] dest_sel,
  input  [31:0] data,
  input  load,
  output [31:0] out_6,
  output [31:0] out_7
);

  wire decoder_1_out0, decoder_1_out1, decoder_1_out2, decoder_1_out3, decoder_1_out4, decoder_1_out5,
       decoder_1_out6, decoder_1_out7, decoder_1_out8, decoder_1_out9, decoder_1_out10, decoder_1_out11,
       decoder_1_out12, decoder_1_out13, decoder_1_out14, decoder_1_out15, delay_1_out_2;
  wire [3:0] bit_extender_1_out, bit_extender_2_out, bit_extender_3_out;
  wire [31:0] register_1_q, register_2_q, register_3_q, register_4_q, register_5_q, register_6_q,
       register_7_q, register_8_q, register_9_q, register_10_q, register_11_q, register_12_q, register_13_q,
       register_14_q, register_15_q, register_16_q;

  Bit_Extender #(.out_width(4)) bit_extender_1 (.in(s0_sel), .out(bit_extender_1_out));
  Bit_Extender #(.out_width(4)) bit_extender_2 (.in(s1_sel), .out(bit_extender_2_out));
  Bit_Extender #(.out_width(4)) bit_extender_3 (.in(dest_sel), .out(bit_extender_3_out));
  Decoder #(.select(4)) decoder_1 (
    .out0(decoder_1_out0), .out1(decoder_1_out1), .out2(decoder_1_out2), .out3(decoder_1_out3),
    .out4(decoder_1_out4), .out5(decoder_1_out5), .out6(decoder_1_out6), .out7(decoder_1_out7),
    .out8(decoder_1_out8), .out9(decoder_1_out9), .out10(decoder_1_out10), .out11(decoder_1_out11),
    .out12(decoder_1_out12), .out13(decoder_1_out13), .out14(decoder_1_out14), .out15(decoder_1_out15),
    .sel(bit_extender_3_out), .en(delay_1_out_2));
  delay delay_1 (.in_1(load), .out_2(delay_1_out_2));
  Register #(.width(32)) register_1 (.D(data), .Q(register_1_q), .clk(decoder_1_out0));  // open: en, clr
  Register #(.width(32)) register_2 (.D(data), .Q(register_2_q), .clk(decoder_1_out1));  // open: en, clr
  Register #(.width(32)) register_3 (.D(data), .Q(register_3_q), .clk(decoder_1_out2));  // open: en, clr
  Register #(.width(32)) register_4 (.D(data), .Q(register_4_q), .clk(decoder_1_out3));  // open: en, clr
  Register #(.width(32)) register_5 (.D(data), .Q(register_5_q), .clk(decoder_1_out4));  // open: en, clr
  Register #(.width(32)) register_6 (.D(data), .Q(register_6_q), .clk(decoder_1_out5));  // open: en, clr
  Register #(.width(32)) register_7 (.D(data), .Q(register_7_q), .clk(decoder_1_out6));  // open: en, clr
  Register #(.width(32)) register_8 (.D(data), .Q(register_8_q), .clk(decoder_1_out7));  // open: en, clr
  Register #(.width(32)) register_9 (.D(data), .Q(register_9_q), .clk(decoder_1_out8));  // open: en, clr
  Register #(.width(32)) register_10 (.D(data), .Q(register_10_q), .clk(decoder_1_out9));  // open: en, clr
  Register #(.width(32)) register_11 (.D(data), .Q(register_11_q), .clk(decoder_1_out10));  // open: en, clr
  Register #(.width(32)) register_12 (.D(data), .Q(register_12_q), .clk(decoder_1_out11));  // open: en, clr
  Register #(.width(32)) register_13 (.D(data), .Q(register_13_q), .clk(decoder_1_out12));  // open: en, clr
  Register #(.width(32)) register_14 (.D(data), .Q(register_14_q), .clk(decoder_1_out13));  // open: en, clr
  Register #(.width(32)) register_15 (.D(data), .Q(register_15_q), .clk(decoder_1_out14));  // open: en, clr
  Register #(.width(32)) register_16 (.D(data), .Q(register_16_q), .clk(decoder_1_out15));  // open: en, clr
  Multiplexer #(.select(4), .width(32)) multiplexer_1 (
    .in0(register_1_q), .in1(register_2_q), .in2(register_3_q), .in3(register_4_q), .in4(register_5_q),
    .in5(register_6_q), .in6(register_7_q), .in7(register_8_q), .in8(register_9_q), .in9(register_10_q),
    .in10(register_11_q), .in11(register_12_q), .in12(register_13_q), .in13(register_14_q),
    .in14(register_15_q), .in15(register_16_q), .out(out_6), .sel(bit_extender_1_out));
  Multiplexer #(.select(4), .width(32)) multiplexer_2 (
    .in0(register_1_q), .in1(register_2_q), .in2(register_3_q), .in3(register_4_q), .in4(register_5_q),
    .in5(register_6_q), .in6(register_7_q), .in7(register_8_q), .in8(register_9_q), .in9(register_10_q),
    .in10(register_11_q), .in11(register_12_q), .in12(register_13_q), .in13(register_14_q),
    .in14(register_15_q), .in15(register_16_q), .out(out_7), .sel(bit_extender_2_out));
endmodule

module delay (
  input  in_1,
  output out_2
);

  wire buffer_1_out, buffer_2_out, buffer_3_out, buffer_4_out, buffer_5_out, buffer_6_out, buffer_7_out,
       buffer_8_out, buffer_9_out, buffer_10_out, buffer_11_out, buffer_12_out, buffer_13_out, buffer_14_out,
       buffer_15_out, buffer_16_out, buffer_17_out, buffer_18_out, buffer_19_out, buffer_20_out,
       buffer_21_out, buffer_22_out, buffer_23_out, buffer_24_out, buffer_25_out, buffer_26_out,
       buffer_27_out, buffer_28_out, buffer_29_out, buffer_30_out, buffer_31_out, buffer_32_out,
       buffer_33_out, buffer_34_out, buffer_35_out, buffer_36_out, buffer_37_out, buffer_38_out,
       buffer_39_out, buffer_40_out, buffer_41_out, buffer_42_out, buffer_43_out, buffer_44_out,
       buffer_45_out, buffer_46_out, buffer_47_out;

  buf buffer_1 (buffer_1_out, in_1);
  buf buffer_2 (buffer_2_out, buffer_1_out);
  buf buffer_3 (buffer_3_out, buffer_2_out);
  buf buffer_4 (buffer_4_out, buffer_5_out);
  buf buffer_5 (buffer_5_out, buffer_6_out);
  buf buffer_6 (buffer_6_out, buffer_7_out);
  buf buffer_7 (buffer_7_out, buffer_15_out);
  buf buffer_8 (buffer_8_out, buffer_4_out);
  buf buffer_9 (buffer_9_out, buffer_8_out);
  buf buffer_10 (buffer_10_out, buffer_9_out);
  buf buffer_11 (buffer_11_out, buffer_3_out);
  buf buffer_12 (buffer_12_out, buffer_11_out);
  buf buffer_13 (buffer_13_out, buffer_12_out);
  buf buffer_14 (buffer_14_out, buffer_13_out);
  buf buffer_15 (buffer_15_out, buffer_16_out);
  buf buffer_16 (buffer_16_out, buffer_17_out);
  buf buffer_17 (buffer_17_out, buffer_18_out);
  buf buffer_18 (buffer_18_out, buffer_27_out);
  buf buffer_19 (buffer_19_out, buffer_10_out);
  buf buffer_20 (buffer_20_out, buffer_19_out);
  buf buffer_21 (buffer_21_out, buffer_20_out);
  buf buffer_22 (buffer_22_out, buffer_21_out);
  buf buffer_23 (buffer_23_out, buffer_14_out);
  buf buffer_24 (buffer_24_out, buffer_23_out);
  buf buffer_25 (buffer_25_out, buffer_24_out);
  buf buffer_26 (buffer_26_out, buffer_25_out);
  buf buffer_27 (buffer_27_out, buffer_28_out);
  buf buffer_28 (buffer_28_out, buffer_29_out);
  buf buffer_29 (buffer_29_out, buffer_30_out);
  buf buffer_30 (buffer_30_out, buffer_39_out);
  buf buffer_31 (buffer_31_out, buffer_22_out);
  buf buffer_32 (buffer_32_out, buffer_31_out);
  buf buffer_33 (buffer_33_out, buffer_32_out);
  buf buffer_34 (buffer_34_out, buffer_33_out);
  buf buffer_35 (buffer_35_out, buffer_26_out);
  buf buffer_36 (buffer_36_out, buffer_35_out);
  buf buffer_37 (buffer_37_out, buffer_36_out);
  buf buffer_38 (buffer_38_out, buffer_37_out);
  buf buffer_39 (buffer_39_out, buffer_40_out);
  buf buffer_40 (buffer_40_out, buffer_41_out);
  buf buffer_41 (buffer_41_out, buffer_42_out);
  buf buffer_42 (buffer_42_out, buffer_47_out);
  buf buffer_43 (buffer_43_out, buffer_34_out);
  buf buffer_44 (buffer_44_out, buffer_43_out);
  buf buffer_45 (buffer_45_out, buffer_44_out);
  buf buffer_46 (buffer_46_out, buffer_45_out);
  buf buffer_47 (buffer_47_out, buffer_38_out);
  buf buffer_48 (out_2, buffer_46_out);
endmodule

module cpu (
  input  [7:0] in_1,
  output [7:0] out_2,
  output [31:0] out_3,
  output out_4
);

  wire alu_1_rsm, and_2_out, clock_1_out, control_1_alu_enable, control_1_alu_init, control_1_del_d_in,
       control_1_flags_sel, control_1_fpu_enable, control_1_fpu_init, control_1_inb_save, control_1_inc_pc,
       control_1_load, control_1_mod0, control_1_mod1, control_1_out_22, control_1_set_a_max,
       control_1_set_a_reg, control_1_set_d_out, control_1_set_fp, control_1_set_ra, control_1_set_sp,
       control_1_stack_offs, control_1_store, control_1_use_imm, control_1_write_pc, controlled_buffer_1_out,
       decoder_1_out0, decoder_2_out7, decoder_2_out8, decoder_2_out9, decoder_2_out10, decoder_2_out11,
       decoder_2_out12, decoder_2_out13, decoder_2_out14, decoder_2_out15, delay_1_out_2, delay_2_out_2,
       delay_3_out_2, delay_4_out_2, delay_5_out_2, delay_6_out_2, delay_8_out_2, delay_10_out_2,
       delay_11_out_2, delay_12_out_2, delay_13_out_2, delay_14_out_2, delay_15_out_2, delay_16_out_2,
       delay_17_out_2, delay_18_out_2, delay_19_out_2, fpu_1_rsm, or_1_out, or_2_out, pull_resistor_2_node;
  wire [1:0] control_1_sel_a, control_1_sel_d_out;
  wire [3:0] control_1_sel_bus_d_s, control_1_sel_inb_reg;
  wire [4:0] bit_extender_2_out;
  wire [7:0] alu_1_flags, dest_q, fpu_1_flags, inst_extra_q, inst_q, multiplexer_12_out, register_5_q,
       register_6_q, s0_q, s1_q;
  wire [31:0] adder_1_out, adder_2_out, adder_3_out, address_q, alu_1_result, bit_extender_1_out,
       bit_extender_3_out, bit_extender_4_out, fp_q, fpu_1_result, multiplexer_1_out, multiplexer_2_out,
       multiplexer_4_out, multiplexer_5_out, multiplexer_6_out, multiplexer_7_out, multiplexer_8_out,
       multiplexer_10_out, multiplexer_11_out, register_1_q, register_2_q, regs_1_out_6, regs_1_out_7,
       ret_a_q, sp_q, stack_offs_q, subtractor_1_out, subtractor_2_out, subtractor_3_out;
  wire [31:16] register_4_q;

  Multiplexer #(.width(32)) multiplexer_1 (
    .in0(sp_q), .in1(multiplexer_10_out), .out(multiplexer_1_out), .sel(control_1_mod0));
  Multiplexer #(.width(32)) multiplexer_2 (
    .in0(sp_q), .in1(multiplexer_10_out), .out(multiplexer_2_out), .sel(control_1_mod0));
  Decoder #(.select(2)) decoder_1 (
    .out0(decoder_1_out0), .sel(control_1_sel_a), .en(delay_4_out_2));  // open: out1, out2, out3
  Register #(.width(32)) stack_offs (.D(multiplexer_10_out), .Q(stack_offs_q), .clk(delay_11_out_2));  // open: en, clr
  Adder #(.width(32)) adder_1 (.a(32'h1), .b(sp_q), .out(adder_1_out));  // open: cin, cout
  Register #(.width(32)) ret_a (.D(multiplexer_2_out), .Q(ret_a_q), .clk(delay_8_out_2));  // open: en, clr
  Multiplexer #(.width(32)) multiplexer_3 (
    .in0(adder_2_out), .in1(multiplexer_5_out), .out(out_3), .sel(decoder_1_out0));
  Register #(.width(32)) address (.D(multiplexer_10_out), .Q(address_q), .clk(delay_12_out_2));  // open: en, clr
  Register #(.width(32)) fp (.D(multiplexer_1_out), .Q(fp_q), .clk(delay_10_out_2));  // open: en, clr
  Multiplexer #(.width(32)) multiplexer_4 (
    .in0(adder_1_out), .in1(multiplexer_10_out), .out(multiplexer_4_out), .sel(control_1_mod0));
  Register #(.width(32)) register_1 (.D(multiplexer_6_out), .Q(register_1_q), .clk(delay_1_out_2));  // open: en, clr
  delay delay_1 (.in_1(or_1_out), .out_2(delay_1_out_2));
  and and_1 (out_4, delay_18_out_2, clock_1_out);
  Multiplexer #(.width(32)) multiplexer_5 (
    .in0(multiplexer_7_out), .in1(multiplexer_8_out), .out(multiplexer_5_out), .sel(delay_4_out_2));
  Register #(.width(32)) sp (.D(multiplexer_4_out), .Q(sp_q), .clk(and_2_out));  // open: en, clr
  and and_2 (and_2_out, clock_1_out, delay_2_out_2);
  Multiplexer #(.width(32)) multiplexer_6 (
    .in0(adder_3_out), .in1(multiplexer_10_out), .out(multiplexer_6_out), .sel(delay_5_out_2));
  or or_1 (or_1_out, delay_5_out_2, delay_6_out_2);
  assign bit_extender_1_out = {{30{1'b0}}, control_1_sel_d_out};  // Bit_Extender bit_extender_1
  Adder #(.width(32)) adder_2 (.a(bit_extender_1_out), .b(multiplexer_5_out), .out(adder_2_out));  // open: cin, cout
  Decoder #(.select(4)) decoder_2 (
    .out7(decoder_2_out7), .out8(decoder_2_out8), .out9(decoder_2_out9), .out10(decoder_2_out10),
    .out11(decoder_2_out11), .out12(decoder_2_out12), .out13(decoder_2_out13), .out14(decoder_2_out14),
    .out15(decoder_2_out15), .sel(control_1_sel_inb_reg), .en(delay_15_out_2));  // open: out0, out1, out2, out3, out4, out5, out6
  Multiplexer #(.select(2), .width(32)) multiplexer_7 (
    .in0(register_1_q), .in1(address_q), .out(multiplexer_7_out), .sel(control_1_sel_a));  // open: in2, in3
  Multiplexer #(.select(2), .width(32)) multiplexer_8 (
    .in0(subtractor_3_out), .in1(subtractor_1_out), .in2(subtractor_2_out), .out(multiplexer_8_out),
    .sel(control_1_sel_a));  // open: in3
  Subtractor #(.width(32)) subtractor_1 (.a(32'hff), .b(fp_q), .out(subtractor_1_out));  // open: bin, bout
  Subtractor #(.width(32)) subtractor_2 (
    .a(subtractor_1_out), .b(stack_offs_q), .out(subtractor_2_out));  // open: bin, bout
  Adder #(.width(32)) adder_3 (.a(register_1_q), .b(32'h1), .out(adder_3_out));  // open: cin, cout
  Register #(.trigger("high")) inst (.D(in_1), .Q(inst_q), .clk(decoder_2_out7));  // open: en, clr
  Subtractor #(.width(32)) subtractor_3 (.a(subtractor_1_out), .b(sp_q), .out(subtractor_3_out));  // open: bin, bout
  Register inst_extra (.D(in_1), .Q(inst_extra_q), .clk(decoder_2_out8));  // open: en, clr
  Register s0 (.D(in_1), .Q(s0_q), .clk(decoder_2_out9));  // open: en, clr
  Register #(.width(32)) register_2 (.D(multiplexer_10_out), .Q(register_2_q), .clk(delay_13_out_2));  // open: en, clr
  Clock clock_1 (.out(clock_1_out));
  Register s1 (.D(in_1), .Q(s1_q), .clk(decoder_2_out10));  // open: en, clr
  Multiplexer #(.select(2), .width(8)) multiplexer_9 (
    .in0(register_2_q[7:0]), .in1(register_2_q[15:8]), .in2(register_2_q[23:16]), .in3(register_2_q[31:24]),
    .out(out_2), .sel(control_1_sel_d_out));
  Register dest (.D(in_1), .Q(dest_q), .clk(decoder_2_out11));  // open: en, clr
  delay delay_2 (.in_1(delay_3_out_2), .out_2(delay_2_out_2));
  delay delay_3 (.in_1(control_1_set_sp), .out_2(delay_3_out_2));
  delay delay_4 (.in_1(control_1_mod1), .out_2(delay_4_out_2));
  delay delay_5 (.in_1(control_1_write_pc), .out_2(delay_5_out_2));
  control control_1 (
    .clk(clock_1_out), .rsm(or_2_out), .in_1(inst_q), .flag_mask(dest_q), .flag(inst_extra_q),
    .flag_ref(multiplexer_12_out), .fpu_init(control_1_fpu_init), .alu_init(control_1_alu_init),
    .stack_offs(control_1_stack_offs), .set_ra(control_1_set_ra), .out_22(control_1_out_22),
    .set_fp(control_1_set_fp), .set_a_max(control_1_set_a_max), .set_a_reg(control_1_set_a_reg),
    .set_d_out(control_1_set_d_out), .del_d_in(control_1_del_d_in), .inb_save(control_1_inb_save),
    .fpu_enable(control_1_fpu_enable), .alu_enable(control_1_alu_enable), .store(control_1_store),
    .load(control_1_load), .set_sp(control_1_set_sp), .mod1(control_1_mod1), .mod0(control_1_mod0),
    .use_imm(control_1_use_imm), .flags_sel(control_1_flags_sel), .sel_a(control_1_sel_a),
    .write_pc(control_1_write_pc), .inc_pc(control_1_inc_pc), .sel_d_out(control_1_sel_d_out),
    .sel_bus_d_s(control_1_sel_bus_d_s), .sel_inb_reg(control_1_sel_inb_reg));
  delay delay_6 (.in_1(control_1_inc_pc), .out_2(delay_6_out_2));
  delay delay_7 (.in_1(control_1_stack_offs));  // open: out_2
  delay delay_8 (.in_1(control_1_set_ra), .out_2(delay_8_out_2));
  Register register_3 (.D(in_1), .Q(register_4_q[31:24]), .clk(decoder_2_out15), .clr(delay_14_out_2));  // open: en
  Register register_4 (.D(in_1), .Q(register_4_q[23:16]), .clk(decoder_2_out14), .clr(delay_14_out_2));  // open: en
  delay delay_9 (.in_1(control_1_out_22));  // open: out_2
  delay delay_10 (.in_1(control_1_set_fp), .out_2(delay_10_out_2));
  delay delay_11 (.in_1(control_1_set_a_max), .out_2(delay_11_out_2));
  delay delay_12 (.in_1(control_1_set_a_reg), .out_2(delay_12_out_2));
  delay delay_13 (.in_1(control_1_set_d_out), .out_2(delay_13_out_2));
  delay delay_14 (.in_1(control_1_del_d_in), .out_2(delay_14_out_2));
  delay delay_15 (.in_1(control_1_inb_save), .out_2(delay_15_out_2));
  delay delay_16 (.in_1(control_1_fpu_enable), .out_2(delay_16_out_2));
  Register register_5 (.D(in_1), .Q(register_5_q), .clk(decoder_2_out13), .clr(delay_14_out_2));  // open: en
  Multiplexer #(.select(4), .width(32)) multiplexer_10 (
    .in0({register_4_q, register_5_q, register_6_q}), .in1(regs_1_out_6), .in2(alu_1_result),
    .in3(bit_extender_3_out), .in6(register_1_q), .in7(ret_a_q), .in8(fpu_1_result),
    .in9(bit_extender_4_out), .out(multiplexer_10_out), .sel(control_1_sel_bus_d_s));  // open: in4, in5, in10, in11, in12, in13, in14, in15
  delay delay_17 (.in_1(control_1_alu_enable), .out_2(delay_17_out_2));
  delay delay_18 (.in_1(control_1_store), .out_2(delay_18_out_2));
  delay delay_19 (.in_1(control_1_load), .out_2(delay_19_out_2));
  Register register_6 (.D(in_1), .Q(register_6_q), .clk(decoder_2_out12), .clr(delay_14_out_2));  // open: en
  Multiplexer #(.width(32)) multiplexer_11 (
    .in0(regs_1_out_6), .in1(multiplexer_10_out), .out(multiplexer_11_out), .sel(control_1_use_imm));
  Bit_Extender #(.out_width(5), .\type ("zero")) bit_extender_2 (.in(inst_extra_q), .out(bit_extender_2_out));
  alu alu_1 (
    .enable(delay_17_out_2), .op(bit_extender_2_out), .a(multiplexer_11_out), .b(regs_1_out_7),
    .init(control_1_alu_init), .clk(clock_1_out), .result(alu_1_result), .flags(alu_1_flags), .rsm(alu_1_rsm));
  fpu fpu_1 (
    .enable(delay_16_out_2), .op(bit_extender_2_out), .a(multiplexer_11_out), .b(regs_1_out_7),
    .init(control_1_fpu_init), .clk(clock_1_out), .result(fpu_1_result), .flags(fpu_1_flags), .rsm(fpu_1_rsm));
  Multiplexer #(.width(8)) multiplexer_12 (
    .in0(alu_1_flags), .in1(fpu_1_flags), .out(multiplexer_12_out), .sel(control_1_flags_sel));
  assign controlled_buffer_1_out = delay_16_out_2 ? fpu_1_rsm : 1'bz;  // Controlled_Buffer controlled_buffer_1
  Pull_Resistor pull_resistor_1 (.node(controlled_buffer_1_out));
  Pull_Resistor pull_resistor_2 (.node(pull_resistor_2_node));
  assign pull_resistor_2_node = delay_17_out_2 ? alu_1_rsm : 1'bz;  // Controlled_Buffer controlled_buffer_2
  or or_2 (or_2_out, controlled_buffer_1_out, pull_resistor_2_node);
  regs regs_1 (
    .s0_sel(s0_q), .s1_sel(s1_q), .dest_sel(dest_q), .data(multiplexer_10_out), .load(delay_19_out_2),
    .out_6(regs_1_out_6), .out_7(regs_1_out_7));
  assign bit_extender_3_out = {{24{1'b0}}, alu_1_flags};  // Bit_Extender bit_extender_3
  assign bit_extender_4_out = {{24{1'b0}}, fpu_1_flags};  // Bit_Extender bit_extender_4
endmodule

module inv_sqrt (
  input  [31:0] in_1,
  output [31:0] aprox,
  output NaN,
  output inpt_zero
);

  wire [31:0] fpmultiplier_1_out, inv_sqrt_raphson_1_improved, shifter_1_out, subtractor_1_out;

  Shifter #(.shift("lr"), .width(32)) shifter_1 (.in(in_1), .\dist (5'b00001), .out(shifter_1_out));
  FPMultiplier fpmultiplier_1 (.a(in_1), .b(32'h3f000000), .out(fpmultiplier_1_out));
  // FPComparator fpcomparator_1: pin names not known; wires that end beside it: in_1, {32{1'b0}}, NaN, inpt_zero
  Subtractor #(.width(32)) subtractor_1 (
    .a(32'h5f3759df), .b(shifter_1_out), .out(subtractor_1_out));  // open: bin, bout
  inv_sqrt_raphson inv_sqrt_raphson_1 (
    .x(subtractor_1_out), .half_initial(fpmultiplier_1_out), .improved(inv_sqrt_raphson_1_improved));
  inv_sqrt_raphson inv_sqrt_raphson_2 (
    .x(inv_sqrt_raphson_1_improved), .half_initial(fpmultiplier_1_out), .improved(aprox));
endmodule

module inv_sqrt_raphson (
  input  [31:0] x,
  input  [31:0] half_initial,
  output [31:0] improved
);

  wire [31:0] fpmultiplier_1_out, fpmultiplier_2_out, fpsubtractor_1_out;

  FPMultiplier fpmultiplier_1 (.a(x), .b(x), .out(fpmultiplier_1_out));
  FPMultiplier fpmultiplier_2 (.a(fpmultiplier_1_out), .b(half_initial), .out(fpmultiplier_2_out));
  FPSubtractor fpsubtractor_1 (.a(32'h3fc00000), .b(fpmultiplier_2_out), .out(fpsubtractor_1_out));
  FPMultiplier fpmultiplier_3 (.a(x), .b(fpsubtractor_1_out), .out(improved));
endmodule

module cordic_trig (
  input  [31:0] ang,
  input  reset,
  input  takt,
  output [31:0] cos,
  output [31:0] sin,
  output [31:0] tan,
  output resume
);

  wire delay_1_out_2, delay_2_out_2, delay_3_out_2, fpcomparator_1_p3, fpcomparator_1_p4, or_1_out, or_2_out,
       or_3_out;
  wire [4:0] i_q;
  wire [31:0] fpadder_1_out, fpdivider_1_out, fpdivider_2_out, fpnegator_1_p2, fpnegator_2_p2,
       fpnegator_3_p2, fpsubtractor_1_out, fpsubtractor_2_out, inttofp_1_p2, multiplexer_1_out,
       multiplexer_2_out, multiplexer_3_out, multiplexer_4_out, multiplexer_5_out, rom_1_data, shifter_1_out,
       z_q;

  delay delay_1 (.in_1(takt), .out_2(delay_1_out_2));
  Multiplexer #(.width(32)) multiplexer_1 (
    .in0(fpsubtractor_1_out), .in1(32'h3f1b74ee), .out(multiplexer_1_out), .sel(reset));
  Register #(.width(32)) x (.D(multiplexer_1_out), .Q(cos), .clk(or_1_out));  // open: en, clr
  or or_1 (or_1_out, delay_2_out_2, takt);
  delay delay_2 (.in_1(reset), .out_2(delay_2_out_2));
  Register #(.width(32)) y (.D(fpadder_1_out), .Q(sin), .clk(takt), .clr(reset));  // open: en
  Multiplexer #(.width(32)) multiplexer_2 (.in0(fpsubtractor_2_out), .in1(ang), .out(multiplexer_2_out), .sel(reset));
  Register #(.width(32)) z (.D(multiplexer_2_out), .Q(z_q), .clk(or_2_out));  // open: en, clr
  or or_2 (or_2_out, delay_3_out_2, takt);
  delay delay_3 (.in_1(reset), .out_2(delay_3_out_2));
  Counter #(.max('h1f), .width(5)) i (.Q(i_q), .carry(resume), .clk(delay_1_out_2));  // open: load, D, count, up, clr
  ROM #(.addrWidth(5), .dataWidth(32)) rom_1 (.addr(i_q), .data(rom_1_data));
  Shifter #(.width(32)) shifter_1 (.in(32'h1), .\dist (i_q), .out(shifter_1_out));
  // FPComparator fpcomparator_1: pin names not known; wires that end beside it: z_q, {32{1'b0}}, fpcomparator_1_p3, fpcomparator_1_p4
  // IntToFP #(.mode("unsigned"), .width(32)) inttofp_1: pin names not known; wires that end beside it: shifter_1_out, inttofp_1_p2
  or or_3 (or_3_out, fpcomparator_1_p3, fpcomparator_1_p4);
  FPDivider fpdivider_1 (.a(cos), .b(inttofp_1_p2), .out(fpdivider_1_out));
  // FPNegator fpnegator_1: pin names not known; wires that end beside it: fpdivider_1_out, fpnegator_1_p2
  FPDivider fpdivider_2 (.a(sin), .b(inttofp_1_p2), .out(fpdivider_2_out));
  // FPNegator fpnegator_2: pin names not known; wires that end beside it: fpdivider_2_out, fpnegator_2_p2
  // FPNegator fpnegator_3: pin names not known; wires that end beside it: rom_1_data, fpnegator_3_p2
  Multiplexer #(.width(32)) multiplexer_3 (
    .in0(fpnegator_1_p2), .in1(fpdivider_1_out), .out(multiplexer_3_out), .sel(or_3_out));
  Multiplexer #(.width(32)) multiplexer_4 (
    .in0(fpnegator_2_p2), .in1(fpdivider_2_out), .out(multiplexer_4_out), .sel(or_3_out));
  Multiplexer #(.width(32)) multiplexer_5 (
    .in0(fpnegator_3_p2), .in1(rom_1_data), .out(multiplexer_5_out), .sel(or_3_out));
  FPAdder fpadder_1 (.a(sin), .b(multiplexer_3_out), .out(fpadder_1_out));
  FPSubtractor fpsubtractor_1 (.a(cos), .b(multiplexer_4_out), .out(fpsubtractor_1_out));
  FPSubtractor fpsubtractor_2 (.a(z_q), .b(multiplexer_5_out), .out(fpsubtractor_2_out));
  FPDivider fpdivider_3 (.a(sin), .b(cos), .out(tan));

  // Notes on the sheet:
  //   contents of rom_1 (hex, n*v repeats v):
  //   3f490fdb 3eed6338 3e7adbb0 3dfeadd5 3d7faade 3cffeaae 3c7ffaab 3bfffeab 3b7fffab 3affffeb 3a7ffffb
  //   39ffffff 39800000 39000000 38800000 38000000 37800000 37000000 36800000 36000000 35800000 35000000
  //   34800000 34000000 33800000 33000000 32800000 32000000 31800000 31000000 30800000 30000000
endmodule

module sqrt (
  input  [31:0] root,
  input  reset,
  input  takt,
  output [31:0] res,
  output resume
);

  wire comparator_1_gt;
  wire [31:0] counter_1_q, fpadder_1_out, fpdivider_1_out, multiplexer_1_out, x_n_q;

  Multiplexer #(.width(32)) multiplexer_1 (.in0(root), .in1(res), .out(multiplexer_1_out), .sel(comparator_1_gt));
  Counter #(.max('h6), .width(32)) counter_1 (
    .Q(counter_1_q), .carry(resume), .clk(takt), .clr(reset));  // open: load, D, count, up
  Register #(.width(32)) x_n (.D(multiplexer_1_out), .Q(x_n_q), .clk(takt), .clr(reset));  // open: en
  Comparator #(.mode("unsigned"), .width(32)) comparator_1 (
    .a(counter_1_q), .b({32{1'b0}}), .gt(comparator_1_gt));  // open: eq, lt
  FPDivider fpdivider_1 (.a(root), .b(x_n_q), .out(fpdivider_1_out));
  FPAdder fpadder_1 (.a(fpdivider_1_out), .b(x_n_q), .out(fpadder_1_out));
  FPMultiplier fpmultiplier_1 (.a(fpadder_1_out), .b(32'h3f000000), .out(res));
  // Probe on res
endmodule

module potenz_float (
  input  [31:0] inpt,
  input  [31:0] power,
  input  reset,
  input  takt,
  output [31:0] res,
  output resume
);

  wire and_1_out, delay_1_out_2, delay_2_out_2, fpcomparator_1_p3, fpcomparator_2_p3, inttofp_1_p2, or_1_out;
  wire [31:0] counter_1_q, fpmultiplier_1_out, fpsubtractor_1_out, multiplexer_1_out, register_1_q,
       register_2_q, register_3_q;

  Register #(.width(32)) register_1 (.D(inpt), .Q(register_1_q), .clk(reset));  // open: en, clr
  Register #(.width(32)) register_2 (.D(power), .Q(register_2_q), .clk(reset));  // open: en, clr
  // FPComparator fpcomparator_1: pin names not known; wires that end beside it: register_2_q, 32'h3f800000, fpcomparator_1_p3
  Multiplexer #(.width(32)) multiplexer_1 (
    .in0(fpmultiplier_1_out), .in1(register_1_q), .out(multiplexer_1_out), .sel(reset));
  Register #(.width(32)) register_3 (.D(multiplexer_1_out), .Q(register_3_q), .clk(or_1_out));  // open: en, clr
  or or_1 (or_1_out, delay_1_out_2, and_1_out);
  delay delay_1 (.in_1(reset), .out_2(delay_1_out_2));
  Counter #(.max('hffffffff), .width(32)) counter_1 (
    .Q(counter_1_q), .clk(and_1_out), .clr(reset));  // open: load, D, count, carry, up
  and and_1 (and_1_out, takt, ~fpcomparator_2_p3);  // AND_Gate
  // IntToFP #(.mode("unsigned"), .width(32)) inttofp_1: pin names not known; wires that end beside it: counter_1_q, inttofp_1_p2
  FPMultiplier fpmultiplier_1 (.a(register_3_q), .b(register_1_q), .out(fpmultiplier_1_out));
  FPSubtractor fpsubtractor_1 (.a(register_2_q), .b(32'h3f800000), .out(fpsubtractor_1_out));
  // FPComparator fpcomparator_2: pin names not known; wires that end beside it: fpsubtractor_1_out, inttofp_1_p2, fpcomparator_2_p3
  Multiplexer #(.width(32)) multiplexer_2 (.in0(register_3_q), .in1(register_1_q), .out(res), .sel(fpcomparator_1_p3));
  delay delay_2 (.in_1(fpcomparator_1_p3), .out_2(delay_2_out_2));
  or or_2 (resume, delay_2_out_2, fpcomparator_2_p3);
endmodule

module potenz_int (
  input  [31:0] inpt,
  input  [31:0] power,
  input  reset,
  input  takt,
  output [31:0] res,
  output resume
);

  wire and_1_out, comparator_1_eq, comparator_2_eq, delay_1_out_2, delay_2_out_2, or_1_out;
  wire [31:0] counter_1_q, multiplexer_1_out, multiplier_1_out, register_1_q, subtractor_1_out;

  Comparator #(.width(32)) comparator_1 (.a(power), .b(32'h1), .eq(comparator_1_eq));  // open: gt, lt
  Multiplexer #(.width(32)) multiplexer_1 (.in0(multiplier_1_out), .in1(inpt), .out(multiplexer_1_out), .sel(reset));
  Register #(.width(32)) register_1 (.D(multiplexer_1_out), .Q(register_1_q), .clk(or_1_out));  // open: en, clr
  or or_1 (or_1_out, delay_1_out_2, and_1_out);
  delay delay_1 (.in_1(reset), .out_2(delay_1_out_2));
  Counter #(.max('hffffffff), .trigger("falling"), .width(32)) counter_1 (
    .Q(counter_1_q), .clk(and_1_out), .clr(reset));  // open: load, D, count, carry, up
  and and_1 (and_1_out, takt, ~comparator_2_eq);  // AND_Gate
  Multiplier #(.width(32)) multiplier_1 (.a(register_1_q), .b(inpt), .out(multiplier_1_out));  // open: cin, cout
  Subtractor #(.width(32)) subtractor_1 (.a(power), .b(32'h1), .out(subtractor_1_out));  // open: bin, bout
  Comparator #(.width(32)) comparator_2 (.a(subtractor_1_out), .b(counter_1_q), .eq(comparator_2_eq));  // open: gt, lt
  Multiplexer #(.width(32)) multiplexer_2 (.in0(register_1_q), .in1(inpt), .out(res), .sel(comparator_1_eq));
  delay delay_2 (.in_1(comparator_1_eq), .out_2(delay_2_out_2));
  or or_2 (resume, delay_2_out_2, comparator_2_eq);
endmodule

module nrt (
  input  [31:0] x,
  input  [31:0] deg,
  input  in_3,
  input  in_4,
  output [31:0] out_5,
  output out_6
);

  wire and_1_out, and_2_out, delay_1_out_2, delay_2_out_2, delay_3_out_2, delay_4_out_2, delay_5_out_2,
       delay_6_out_2, delay_7_out_2, delay_8_out_2, fpcomparator_1_p3, fpcomparator_2_p3, fpcomparator_3_p3,
       fpcomparator_4_p3, not_1_out, not_2_out, not_3_out, not_4_out, or_1_out, or_2_out,
       potenz_float_1_resume, pull_resistor_1_node, pull_resistor_2_node, pull_resistor_3_node;
  wire [31:0] fpadder_1_out, fpdivider_1_out, fpdivider_2_out, fpsubtractor_1_out, fpsubtractor_2_out,
       multiplexer_1_out, multiplexer_2_out, multiplexer_3_out, potenz_float_1_res, register_1_q,
       register_2_q;

  not not_1 (not_1_out, out_6);
  Pull_Resistor pull_resistor_1 (.node(pull_resistor_1_node));
  assign pull_resistor_1_node = not_1_out ? in_4 : 1'bz;  // Controlled_Buffer controlled_buffer_1
  not not_2 (not_2_out, pull_resistor_1_node);
  delay delay_1 (.in_1(and_1_out), .out_2(delay_1_out_2));
  and and_1 (and_1_out, not_2_out, potenz_float_1_resume);
  delay delay_2 (.in_1(delay_1_out_2), .out_2(delay_2_out_2));
  delay delay_3 (.in_1(delay_2_out_2), .out_2(delay_3_out_2));
  not not_3 (not_3_out, out_6);
  Pull_Resistor pull_resistor_2 (.node(pull_resistor_2_node));
  assign pull_resistor_2_node = not_3_out ? delay_3_out_2 : 1'bz;  // Controlled_Buffer controlled_buffer_2
  or or_1 (or_1_out, pull_resistor_2_node, in_3);
  delay delay_4 (.in_1(or_1_out), .out_2(delay_4_out_2));
  FPDivider fpdivider_1 (.a(x), .b(32'h40000000), .out(fpdivider_1_out));
  potenz_float potenz_float_1 (
    .inpt(register_2_q), .power(deg), .reset(delay_5_out_2), .takt(pull_resistor_1_node),
    .res(potenz_float_1_res), .resume(potenz_float_1_resume));
  delay delay_5 (.in_1(delay_4_out_2), .out_2(delay_5_out_2));
  Multiplexer #(.width(32)) multiplexer_1 (
    .in0(fpdivider_2_out), .in1(fpdivider_1_out), .out(multiplexer_1_out), .sel(in_3));
  Multiplexer #(.width(32)) multiplexer_2 (
    .in0(multiplexer_3_out), .in1(fpdivider_1_out), .out(multiplexer_2_out), .sel(in_3));
  delay delay_6 (.in_1(or_2_out), .out_2(delay_6_out_2));
  Pull_Resistor pull_resistor_3 (.node(pull_resistor_3_node));
  assign pull_resistor_3_node = not_4_out ? potenz_float_1_resume : 1'bz;  // Controlled_Buffer controlled_buffer_3
  or or_2 (or_2_out, pull_resistor_3_node, in_3);
  not not_4 (not_4_out, delay_7_out_2);
  delay delay_7 (.in_1(delay_8_out_2), .out_2(delay_7_out_2));
  delay delay_8 (.in_1(out_6), .out_2(delay_8_out_2));
  Register #(.width(32)) register_1 (.D(multiplexer_1_out), .Q(register_1_q), .clk(delay_6_out_2));  // open: en, clr
  Register #(.width(32)) register_2 (.D(multiplexer_2_out), .Q(register_2_q), .clk(delay_6_out_2));  // open: en, clr
  Register #(.width(32)) register_3 (.D(register_2_q), .Q(out_5), .clk(out_6), .clr(in_3));  // open: en
  FPDivider fpdivider_2 (.a(register_1_q), .b(32'h40000000), .out(fpdivider_2_out));
  FPSubtractor fpsubtractor_1 (.a(register_2_q), .b(register_1_q), .out(fpsubtractor_1_out));
  Multiplexer #(.width(32)) multiplexer_3 (
    .in0(fpsubtractor_1_out), .in1(fpadder_1_out), .out(multiplexer_3_out), .sel(fpcomparator_1_p3));
  FPAdder fpadder_1 (.a(register_1_q), .b(register_2_q), .out(fpadder_1_out));
  // FPComparator fpcomparator_1: pin names not known; wires that end beside it: x, potenz_float_1_res, fpcomparator_1_p3
  FPSubtractor fpsubtractor_2 (.a(x), .b(potenz_float_1_res), .out(fpsubtractor_2_out));
  // FPComparator fpcomparator_2: pin names not known; wires that end beside it: register_1_q, {32{1'b0}}, fpcomparator_2_p3
  // FPComparator fpcomparator_3: pin names not known; wires that end beside it: fpsubtractor_2_out, 32'h3a03126f, fpcomparator_3_p3
  and and_2 (and_2_out, fpcomparator_3_p3, potenz_float_1_resume, fpcomparator_4_p3);
  // FPComparator fpcomparator_4: pin names not known; wires that end beside it: fpsubtractor_2_out, 32'hba03126f, fpcomparator_4_p3
  or or_3 (out_6, and_2_out, fpcomparator_2_p3);
endmodule

module ln (
  input  [31:0] x,
  input  reset,
  input  clk,
  output [31:0] out_4,
  output resume
);

  wire and_1_out, delay_1_out_2, delay_2_out_2, delay_3_out_2, delay_4_out_2, delay_5_out_2, delay_6_out_2,
       delay_7_out_2, delay_8_out_2, fpcomparator_1_p3, i_carry, not_1_out, or_1_out, or_2_out,
       pull_resistor_1_node, pull_resistor_2_node;
  wire [3:0] i_q;
  wire [31:0] fpadder_1_out, fpdivider_1_out, fpdivider_2_out, k_q, multiplexer_1_out, multiplexer_2_out,
       rom_1_data, z_q;

  Pull_Resistor pull_resistor_1 (.node(pull_resistor_1_node));
  assign pull_resistor_1_node = not_1_out ? clk : 1'bz;  // Controlled_Buffer controlled_buffer_1
  not not_1 (not_1_out, resume);
  Multiplexer #(.width(32)) multiplexer_1 (
    .in0(fpdivider_1_out), .in1(32'h3f800000), .out(multiplexer_1_out), .sel(reset));
  Register #(.width(32)) k (.D(multiplexer_1_out), .Q(k_q), .clk(or_1_out));  // open: en, clr
  or or_1 (or_1_out, delay_1_out_2, pull_resistor_2_node);
  delay delay_1 (.in_1(reset), .out_2(delay_1_out_2));
  Multiplexer #(.width(32)) multiplexer_2 (.in0(fpdivider_2_out), .in1(x), .out(multiplexer_2_out), .sel(reset));
  Register #(.width(32)) z (.D(multiplexer_2_out), .Q(z_q), .clk(or_2_out));  // open: en, clr
  or or_2 (or_2_out, delay_3_out_2, delay_2_out_2);
  delay delay_2 (.in_1(delay_4_out_2), .out_2(delay_2_out_2));
  delay delay_3 (.in_1(reset), .out_2(delay_3_out_2));
  delay delay_4 (.in_1(pull_resistor_1_node), .out_2(delay_4_out_2));
  Register #(.width(32)) ln_x (.D(fpadder_1_out), .Q(out_4), .clk(pull_resistor_1_node), .clr(reset));  // open: en
  Counter #(.max('hf), .trigger("falling"), .width(4)) i (
    .Q(i_q), .carry(i_carry), .clk(and_1_out), .clr(reset));  // open: load, D, count, up
  and and_1 (and_1_out, pull_resistor_1_node, delay_5_out_2);
  delay delay_5 (.in_1(delay_6_out_2), .out_2(delay_5_out_2));
  delay delay_6 (.in_1(fpcomparator_1_p3), .out_2(delay_6_out_2));
  and and_2 (resume, fpcomparator_1_p3, i_carry);
  FPDivider fpdivider_1 (.a(k_q), .b(32'h40000000), .out(fpdivider_1_out));
  FPDivider fpdivider_2 (.a(z_q), .b(rom_1_data), .out(fpdivider_2_out));
  FPAdder fpadder_1 (.a(out_4), .b(k_q), .out(fpadder_1_out));
  ROM #(.addrWidth(4), .dataWidth(32)) rom_1 (.addr(i_q), .data(rom_1_data));
  Pull_Resistor pull_resistor_2 (.node(pull_resistor_2_node));
  assign pull_resistor_2_node = delay_7_out_2 ? delay_4_out_2 : 1'bz;  // Controlled_Buffer controlled_buffer_2
  delay delay_7 (.in_1(delay_8_out_2), .out_2(delay_7_out_2));
  // FPComparator fpcomparator_1: pin names not known; wires that end beside it: fpdivider_2_out, rom_1_data, fpcomparator_1_p3
  delay delay_8 (.in_1(fpcomparator_1_p3), .out_2(delay_8_out_2));

  // Notes on the sheet:
  //   contents of rom_1 (hex, n*v repeats v):
  //   402df854 3fd3094c 3fa45af2 3f910b02 3f88415b 3f84102b 3f820405 3f810101 3f808040 3f804010 3f802004
  //   3f801001 3f800800 3f800400 3f800200 3f800100
endmodule
